// Digital circuit NuPDP.dig as structural Verilog
module NuPDP (
  input  MAX,
  input  [11:0] SWITCH,
  input  _25Hz,
  input  [11:0] in_4,
  input  in_5,
  input  _1Hz,
  input  clk
);

  wire _2_out, _74ls74_2__1nq, _74ls74_2__1q, _74ls74_2__2q, _74ls74_3__1q, _74ls74_3__2q, _74ls161_1_rco,
       _74ls161_2_rco, _74ls273_7_q0, _74ls273_7_q1, _74ls273_7_q2, _74ls273_7_q3, _74ls273_7_q4,
       _74ls273_7_q5, _74ls273_7_q6, _74ls273_7_q7, _74ls273_8_q0, _74ls273_8_q1, _74ls273_8_q2,
       _74ls273_8_q3, _74ls283_1_c_out, _74ls283_1_s1, _74ls283_1_s2, _74ls283_1_s3, _74ls283_1_s4,
       _74ls283_2_c_out, _74ls283_2_s1, _74ls283_2_s2, _74ls283_2_s3, _74ls283_2_s4, _74ls283_3_s1,
       _74ls283_3_s2, _74ls283_3_s3, _74ls283_3_s4, _74ls283_4_c_out, _74ls283_4_s1, _74ls283_4_s2,
       _74ls283_4_s3, _74ls283_4_s4, _74ls283_5_c_out, _74ls283_5_s1, _74ls283_5_s2, _74ls283_5_s3,
       _74ls283_5_s4, _74ls283_6_s1, _74ls283_6_s2, _74ls283_6_s3, _74ls283_6_s4, aiFinished, ALU_Lin,
       ALU_Lout, AND, and_3_out, and_4_out, and_5_out, and_6_out, and_7_out, and_8_out, and_9_out,
       and_11_out, and_15_out, and_18_out, and_19_out, and_20_out, and_21_out, and_22_out, and_23_out,
       and_24_out, and_26_out, and_29_out, and_36_out, and_38_out, and_40_out, and_41_out, and_73_out,
       and_75_out, and_80_out, and_81_out, and_82_out, and_84_out, and_85_out, and_87_out, and_88_out,
       and_89_out, and_91_out, and_93_out, and_94_out, and_96_out, and_97_out, and_100_out, and_103_out,
       and_108_out, and_109_out, and_112_out, and_113_out, and_138_out, and_139_out, and_140_out,
       and_141_out, and_142_out, and_143_out, and_144_out, and_145_out, and_146_out, and_147_out,
       and_148_out, and_149_out, and_150_out, AND_TAD_d3, AND_TAD_d4, AND_TAD_d5, AND_TAD_d6, AND_TAD_p1,
       AND_TAD_p2, AND_TAD_p3, AND_TAD_p4, AND_TAD_p5, AND_TAD_p6, AND_TAD_p7, BP, BSW, CAF, CAF_6007,
       ckACC_2, ckACC_4, ckACC_5, ckACC_gtf, ckACC_iot1, ckACC_mop1, ckACC_mop2, ckDBUStoABUS_andtad,
       ckDBUStoABUS_dca, ckDBUStoABUS_isz, ckDBUStoABUS_jmp, ckDBUStoABUS_jms, ckIncDBUS__ai,
       ckIncDBUS__isz2, ckIncDBUS_isz1, ckIncPC_irq1, ckIncPC_jms1, ckIncPC_LoadIR, ckIR_0, ckIR_irq,
       ckIR_LoadIR, ckIRQhandler, ckMQ_1, ckSetPC_0, ckSetPC_jmp, ckSetPC_jms, CLA, CLA_1, CLA_2, CLA_3,
       CLA_4, CLK_t, CLL, clrPC_irq, CMA, CML, CODE_lsb, CODE_mid, CODE_msb, comparator_1_eq, d_ff_2_q,
       d_ff_3_nq, d_ff_as_1_q, d_ff_as_2_nq, d_ff_as_2_q, DCA, DCA_d1, DCA_d2, DCA_d3, DCA_d4, DCA_d5,
       DCA_p1, DCA_p2, DCA_p3, DCA_p4, DCA_p5, DCA_p7, delay_3_out, enACCclear_dca, enACCclear_iot1,
       enACCclear_mop3a, enACCtoDBUS_2, enACCtoDBUS_dca, enALUadd, enALUand, enALUor_mop2, enALUtoACC_andtad,
       enALUtoACC_mop1, enALUtoACC_mop2, enDBUStoABUS_andtad, enDBUStoABUS_dca, enIncToDBUS_ai,
       enIncToDBUS_isz1, enIncToDBUS_isz2, enINSTRtoABUS_ai, enINSTRtoABUS_andtad, enINSTRtoABUS_dca,
       enINSTRtoABUS_isz, enINSTRtoABUS_jmp, enINSTRtoABUS_jms, enIRQ, enPCtoABUS_0, enPCtoABUS_irq,
       enPCtoABUS_LoadIR, enPCtoABUS_mop2, enPCtoDBUS_irq, enRAMtoDBUS_ai, enRAMtoDBUS_andtad,
       enRAMtoDBUS_dca, enRAMtoDBUS_isz, enRAMtoDBUS_jmp, enRAMtoDBUS_jms, fAccZero, fAutoinc, fDBUSisZero,
       fGIE, fIndirect, fIrqDly, fKBD, fPendInt, fPRN, fSkip, GTF_6004, H_out, HLT, IAC, IAC_carryout, iDone,
       iDone1, iDoneBeforeIRQ, ii, ii_dca, ii_iot, ii_isz, ii_jmp, ii_jms, ii_mop1, ii_mop2, ii_mop3a, INC1,
       INC1_iot, INC1_isz, INC1_mop2, INC1_mop3a, INC2, INC2_iot1, INC2_iot2, INC2_iot3, INC2_iot4,
       INC2_iot5, INC2_isz, INC2_mop2, INDIRECT, inhibitIR, INTE_nq, IOF_6002, ION_6001, IOT, IOT_CPU,
       IOT_d1, IOT_d2, IOT_d4, IOT_d5, IOT_d6, IOT_d7, IOT_d8, IOT_HISPEEDPUNCH, IOT_HISPEEDREADER, IOT_p2,
       IOT_p3, IOT_p4, IOT_p5, IOT_p6, IOT_p7, IOT_TTYPUNCH, IOT_TTYREADER, isCurrPage, ISZ, ISZ_ISZi_d1,
       ISZ_ISZi_d4, ISZ_ISZi_p1, ISZ_ISZi_p2, ISZ_ISZi_p3, JMP, JMP_JMPi_d2, JMP_JMPi_d3, JMP_JMPi_d4,
       JMP_JMPi_d5, JMP_JMPi_d6, JMP_JMPi_p1, JMP_JMPi_p2, JMP_JMPi_p3, JMP_JMPi_p4, JMP_JMPi_p5,
       JMP_JMPi_p6, JMP_JMPi_p7, JMS, JMS_JMSi_d2, JMS_JMSi_d3, JMS_JMSi_d4, JMS_JMSi_d6, JMS_JMSi_d7,
       JMS_JMSi_d8, JMS_JMSi_p1, JMS_JMSi_p2, JMS_JMSi_p5, JMS_JMSi_p6, JMS_JMSi_p7, KCC_6032, KCF_6030, KIE,
       KIE_6035, KRB, KRB_6036, KRS_6034, KSF_6031, L6, LINK, M_out, MOP1, MOP1_d4, MOP1_d5, MOP1_d6,
       MOP1_d7, MOP1_d8, MOP1_p1, MOP1_p2, MOP1_p3, MOP1_p4, MOP1_p5, MOP1_p6, MOP1_p7, MOP2, MOP2_d2,
       MOP2_d4, MOP2_d5, MOP2_d7, MOP2_d8, MOP2_p1, MOP2_p3, MOP2_p4, MOP2_p5, MOP2_p6, MOP2_p7, MOP3,
       MOP3_d1, MOP3_d2, MOP3_d3, MOP3_d5, MOP3_d6, MOP3_d7, MOP3_p2, MOP3_p3, MOP3_p4, MOP3_p5, MOP3_p6,
       MOP3_p7, MQA, MQL, nand_1_out, nand_2_out, nand_3_out, nand_4_out, nand_5_out, nand_6_out, nor_1_out,
       nor_2_out, not_1_out, not_2_out, not_3_out, not_4_out, not_5_out, not_7_out, not_8_out, not_9_out,
       not_10_out, not_11_out, not_12_out, not_13_out, not_14_out, not_15_out, not_16_out, not_17_out,
       not_18_out, not_19_out, not_20_out, not_21_out, not_22_out, not_24_out, not_25_out, not_26_out,
       not_27_out, not_28_out, not_29_out, not_30_out, not_31_out, not_32_out, not_33_out, not_34_out,
       not_35_out, not_36_out, not_37_out, not_38_out, not_39_out, not_40_out, not_41_out, not_42_out,
       not_43_out, not_44_out, not_45_out, not_46_out, not_48_out, not_50_out, oneshot_1_o, oneshot_2_o,
       oneshot_3_o, oneshot_4_o, oneshot_5_o, oneshot_6_o, oneshot_7_o, oneshot_8_o, oneshot_9_o, or_1_out,
       or_4_out, or_5_out, or_6_out, or_7_out, or_8_out, or_9_out, or_10_out, or_11_out, or_12_out,
       or_13_out, or_14_out, or_15_out, or_16_out, or_17_out, or_18_out, or_19_out, or_20_out, or_22_out,
       or_23_out, or_24_out, or_25_out, or_27_out, or_32_out, or_33_out, or_34_out, or_43_out, or_44_out,
       or_46_out, or_47_out, or_48_out, or_49_out, or_50_out, or_51_out, or_52_out, or_53_out, or_54_out,
       or_55_out, or_57_out, or_58_out, or_59_out, or_60_out, or_61_out, or_62_out, or_63_out, or_64_out,
       or_65_out, or_66_out, or_67_out, or_68_out, or_69_out, or_70_out, or_71_out, or_72_out, or_73_out,
       or_74_out, or_75_out, or_76_out, or_77_out, or_78_out, or_79_out, or_80_out, or_81_out, or_82_out,
       R_out, RESET, reset_1_out, rs_ff_as_2_q, rs_ff_as_3_q, RTF_INTEclr, RTF_INTEset, RTF_linkClr,
       RTF_linkSet, S_out, sequencer_1_d2, sequencer_1_d3, sequencer_1_d4, sequencer_1_d5, sequencer_1_d6,
       sequencer_1_d7, sequencer_1_p3, sequencer_1_p4, sequencer_1_p5, sequencer_1_p6, sequencer_1_p7,
       sequencer_2_d1, sequencer_2_d2, sequencer_2_d3, sequencer_2_d5, sequencer_2_d6, sequencer_2_d7,
       sequencer_2_p2, sequencer_2_p4, sequencer_2_p7, STOP, t_ff_1_q, T_out, tty_1_rxavail, tty_1_txdone,
       TTY_IE_q, weRAM_ai, weRAM_dca, weRAM_irq, xor_1_out, xor_4_out, xor_5_out, xor_6_out, xor_7_out,
       xor_8_out, xor_9_out, xor_10_out, xor_11_out, xor_12_out, xor_13_out, xor_14_out, xor_15_out, ZEROPAGE;
  wire [5:0] L_PRN;
  wire [5:2] L_IRQ;
  wire [7:1] L_CPU;
  wire [8:1] L_OPR2;
  wire [10:1] L_OPR1;
  wire [10:3] L_GEN;
  wire [11:0] ABUS, ACC, ALU_out, and_114_out, and_126_out, IR, IRA, MQ, OBUS, PC, ramspy_1_o;
  wire [12:0] L_OPR3;
  wire [15:0] CharRom3x_d_2, CharRom3x_d_3;
  wire [19:0] counter_1_out, d_ff_1_q;
  wire [24:0] DAW;
  wire [50:0] CharRom3x_d;

  // Probe on ABUS
  PullDown #(.Bits(12)) pulldown_1 (.out(ABUS));
  or or_1 (or_1_out, ckIR_0, ckIR_irq, ckIR_LoadIR);
  OneShot oneshot_1 (.i(_1Hz), .o(oneshot_1_o));
  Comparator #(.Bits(12)) comparator_1 (.a(in_4), .b(IRA), .eq(comparator_1_eq));  // open: gt, lt
  T_FF t_ff_1 (.T(1'b1), .C(oneshot_1_o), .Q(t_ff_1_q));  // open: nQ
  or or_2 (DAW[24], weRAM_dca, enIncToDBUS_isz1, enIncToDBUS_isz2, weRAM_irq, ckIncPC_jms1, weRAM_ai);
  or or_3 (L6, ckSetPC_0, enPCtoABUS_LoadIR, enRAMtoDBUS_jmp, enRAMtoDBUS_jms, enPCtoABUS_irq, enRAMtoDBUS_andtad, enRAMtoDBUS_ai, enRAMtoDBUS_isz, enRAMtoDBUS_dca);
  or or_4 (or_4_out, enIncToDBUS_isz1, enIncToDBUS_isz2, enIncToDBUS_ai);
  or or_5 (or_5_out, ckIncDBUS_isz1, ckIncDBUS__isz2, ckIncDBUS__ai);
  and and_1 (BP, comparator_1_eq, in_5, or_1_out);
  Counter #(.Bits(20)) counter_1 (.en(1'b1), .C(iDone), .clr(t_ff_1_q), .out(counter_1_out));  // open: ovf
  not not_1 (not_1_out, or_4_out);
  _74LS283 _74ls283_1 (
    .A1(DAW[0]), .A2(DAW[1]), .A3(DAW[2]), .A4(DAW[3]), .B1(1'b0), .B2(1'b0), .B3(1'b0), .B4(1'b0),
    .S1(_74ls283_1_s1), .S2(_74ls283_1_s2), .S3(_74ls283_1_s3), .S4(_74ls283_1_s4), .C_in(1'b1),
    .C_out(_74ls283_1_c_out));
  _74LS283 _74ls283_2 (
    .A1(DAW[4]), .A2(DAW[5]), .A3(DAW[6]), .A4(DAW[7]), .B1(1'b0), .B2(1'b0), .B3(1'b0), .B4(1'b0),
    .S1(_74ls283_2_s1), .S2(_74ls283_2_s2), .S3(_74ls283_2_s3), .S4(_74ls283_2_s4), .C_in(_74ls283_1_c_out),
    .C_out(_74ls283_2_c_out));
  _74LS283 _74ls283_3 (
    .A1(DAW[8]), .A2(DAW[9]), .A3(DAW[10]), .A4(DAW[11]), .B1(1'b0), .B2(1'b0), .B3(1'b0), .B4(1'b0),
    .S1(_74ls283_3_s1), .S2(_74ls283_3_s2), .S3(_74ls283_3_s3), .S4(_74ls283_3_s4), .C_in(_74ls283_2_c_out));  // open: C_out
  // Probe on BP
  _74LS273 _74ls273_1 (
    .CP(or_1_out), .nMR(1'b1), .D0(PC[0]), .D1(PC[1]), .D2(PC[2]), .D3(PC[3]), .D4(PC[4]), .D5(PC[5]),
    .D6(PC[6]), .D7(PC[7]), .Q0(IRA[0]), .Q1(IRA[1]), .Q2(IRA[2]), .Q3(IRA[3]), .Q4(IRA[4]), .Q5(IRA[5]),
    .Q6(IRA[6]), .Q7(IRA[7]));
  _74LS273 _74ls273_2 (
    .CP(or_1_out), .nMR(1'b1), .D0(PC[8]), .D1(PC[9]), .D2(PC[10]), .D3(PC[11]), .D4(1'b0), .D5(1'b0),
    .D6(1'b0), .D7(1'b0), .Q0(IRA[8]), .Q1(IRA[9]), .Q2(IRA[10]), .Q3(IRA[11]));  // open: Q4, Q5, Q6, Q7
  _74LS273 _74ls273_3 (
    .CP(or_1_out), .nMR(1'b1), .D0(DAW[0]), .D1(DAW[1]), .D2(DAW[2]), .D3(DAW[3]), .D4(DAW[4]), .D5(DAW[5]),
    .D6(DAW[6]), .D7(DAW[7]), .Q0(IR[0]), .Q1(IR[1]), .Q2(IR[2]), .Q3(IR[3]), .Q4(IR[4]), .Q5(IR[5]),
    .Q6(IR[6]), .Q7(IR[7]));
  _74LS273 _74ls273_4 (
    .CP(or_1_out), .nMR(1'b1), .D0(DAW[8]), .D1(DAW[9]), .D2(DAW[10]), .D3(DAW[11]), .D4(1'b0), .D5(1'b0),
    .D6(1'b0), .D7(1'b0), .Q0(IR[8]), .Q1(IR[9]), .Q2(IR[10]), .Q3(IR[11]));  // open: Q4, Q5, Q6, Q7
  Reset #(.invertOutput("false")) reset_1 (.out(reset_1_out));
  not not_2 (not_2_out, DAW[24]);
  not not_3 (not_3_out, L6);
  not not_4 (not_4_out, not_1_out);
  D_FF #(.Bits(20)) d_ff_1 (.D(counter_1_out), .C(t_ff_1_q), .Q(d_ff_1_q));  // open: nQ
  EEPROM #(.AddrBits(12), .isProgramMemory("true"), .Bits(12)) eeprom_1 (
    .A(ABUS), .CS(~reset_1_out), .WE(~not_2_out), .OE(~not_3_out), .D(DAW[11:0]));
  // Probe on d_ff_1_q
  // Probe on DAW[11:0]
  not not_5 (not_5_out, not_4_out);
  _74ls374 _74ls374_1 (
    .Q0(DAW[0]), .Q1(DAW[1]), .Q2(DAW[2]), .Q3(DAW[3]), .Q4(DAW[4]), .Q5(DAW[5]), .Q6(DAW[6]), .Q7(DAW[7]),
    .nOC(not_5_out), .CLK(or_5_out), .D0(_74ls283_1_s1), .D1(_74ls283_1_s2), .D2(_74ls283_1_s3),
    .D3(_74ls283_1_s4), .D4(_74ls283_2_s1), .D5(_74ls283_2_s2), .D6(_74ls283_2_s3), .D7(_74ls283_2_s4));  // open: iv
  _74ls374 _74ls374_2 (
    .Q0(DAW[8]), .Q1(DAW[9]), .Q2(DAW[10]), .Q3(DAW[11]), .nOC(not_5_out), .CLK(or_5_out),
    .D0(_74ls283_3_s1), .D1(_74ls283_3_s2), .D2(_74ls283_3_s3), .D3(_74ls283_3_s4), .D4(1'b0), .D5(1'b0),
    .D6(1'b0), .D7(1'b0));  // open: Q4, Q5, Q6, Q7, iv
  or or_6 (or_6_out, DAW[0], DAW[1], DAW[2], DAW[3], DAW[4], DAW[5], DAW[6], DAW[7], DAW[8], DAW[9], DAW[10], DAW[11]);
  SixteenSeg sixteenseg_1 (.led(CharRom3x_d[15:0]), .dp(CharRom3x_d[50]));
  ROM #(.AddrBits(12), .Bits(51)) CharRom3x (
    .A(IR), .sel(1'b1),
    .D({CharRom3x_d[50], fIndirect, isCurrPage, CharRom3x_d_3, CharRom3x_d_2, CharRom3x_d[15:0]}));
  LED led_1 (.in(AND));
  LED led_2 (.in(fGIE));
  LED led_3 (.in(L_OPR1[10]));
  LED led_4 (.in(CLA_2));
  LED led_5 (.in(L_OPR3[12]));
  LED led_6 (.in(L_CPU[7]));
  LED led_7 (.in(KCF_6030));
  LED led_8 (.in(L_PRN[5]));
  not not_6 (fDBUSisZero, or_6_out);
  SixteenSeg sixteenseg_2 (.led(CharRom3x_d_2), .dp(CharRom3x_d[50]));
  LED led_9 (.in(L_GEN[10]));
  LED led_10 (.in(L_IRQ[5]));
  LED led_11 (.in(CLA_1));
  LED led_12 (.in(L_OPR2[8]));
  LED led_13 (.in(CLA_3));
  LED led_14 (.in(ION_6001));
  LED led_15 (.in(KSF_6031));
  LED led_16 (.in(L_PRN[4]));
  SixteenSeg sixteenseg_3 (.led(CharRom3x_d_3), .dp(CharRom3x_d[50]));
  LED led_17 (.in(ISZ));
  LED led_18 (.in(DCA));
  LED led_19 (.in(fIrqDly));
  LED led_20 (.in(enIRQ));
  LED led_21 (.in(CLL));
  LED led_22 (.in(CMA));
  LED led_23 (.in(L_OPR2[6]));
  LED led_24 (.in(L_OPR2[7]));
  LED led_25 (.in(L_OPR3[10]));
  LED led_26 (.in(L_OPR3[9]));
  LED led_27 (.in(IOF_6002));
  LED led_28 (.in(L_CPU[4]));
  LED led_29 (.in(KCC_6032));
  LED led_30 (.in(KRS_6034));
  LED led_31 (.in(L_PRN[3]));
  LED led_32 (.in(L_PRN[2]));
  Seven_Seg_Hex seven_seg_hex_1 (.d({3'b000, IR[6]}), .dp(1'b0));
  LED CURRENT_PAGE (.in(isCurrPage));
  LED u_INDIRECT (.in(fIndirect));
  LED led_33 (.in(JMS));
  LED led_34 (.in(L_IRQ[2]));
  LED led_35 (.in(CML));
  LED led_36 (.in(L_OPR2[5]));
  LED led_37 (.in(L_OPR3[8]));
  LED led_38 (.in(GTF_6004));
  LED led_39 (.in(KIE_6035));
  LED led_40 (.in(L_PRN[1]));
  Seven_Seg_Hex seven_seg_hex_2 (.d({1'b0, IR[5:3]}), .dp(1'b0));
  and and_2 (fAutoinc, fIndirect, IR[3], not_7_out, not_8_out, not_9_out, not_10_out);
  not not_7 (not_7_out, IR[4]);
  not not_8 (not_8_out, IR[5]);
  not not_9 (not_9_out, IR[6]);
  not not_10 (not_10_out, isCurrPage);
  LED led_41 (.in(JMP));
  LED led_42 (.in(fKBD));
  LED led_43 (.in(IAC));
  LED led_44 (.in(L_OPR2[4]));
  LED led_45 (.in(L_OPR3[7]));
  LED led_46 (.in(L_CPU[2]));
  LED led_47 (.in(KRB_6036));
  LED led_48 (.in(L_PRN[0]));
  Seven_Seg_Hex seven_seg_hex_3 (.d({1'b0, IR[2:0]}), .dp(1'b0));
  LED led_49 (.in(IOT));
  LED led_50 (.in(L_GEN[4]));
  LED led_51 (.in(fPRN));
  LED led_52 (.in(L_OPR1[4]));
  LED led_53 (.in(L_OPR1[3]));
  LED led_54 (.in(L_OPR2[2]));
  LED led_55 (.in(L_OPR2[3]));
  LED led_56 (.in(L_OPR3[6]));
  LED led_57 (.in(L_OPR3[5]));
  LED led_58 (.in(L_CPU[1]));
  LED led_59 (.in(CAF_6007));
  or or_7 (or_7_out, enDBUStoABUS_andtad, ckDBUStoABUS_jmp, ckDBUStoABUS_jms, ckDBUStoABUS_isz, enDBUStoABUS_dca);
  or or_8 (or_8_out, ckDBUStoABUS_andtad, ckDBUStoABUS_jmp, ckDBUStoABUS_jms, ckDBUStoABUS_isz, ckDBUStoABUS_dca);
  LED led_60 (.in(L_GEN[3]));
  LED led_61 (.in(L_OPR1[2]));
  LED led_62 (.in(L_OPR2[1]));
  LED led_63 (.in(L_OPR3[4]));
  LED led_64 (.in(fIndirect));
  LED led_65 (.in(L_OPR1[1]));
  LED led_66 (.in(HLT));
  LED led_67 (.in(L_OPR3[3]));
  RAMSPY ramspy_1 (.Trig({12{1'b0}}), .DAW({DAW[24], ABUS, DAW[11:0]}), .O(ramspy_1_o));
  // Probe on iDone
  LED led_68 (.in(fAutoinc));
  LED led_69 (.in(isCurrPage));
  LED led_70 (.in(BSW));
  LED led_71 (.in(L_OPR3[2]));
  LED led_72 (.in(L_OPR3[1]));
  PullDown pulldown_2 (.out(L_IRQ[2]));
  PullDown pulldown_3 (.out(L_IRQ[5]));
  or or_9 (or_9_out, enINSTRtoABUS_jmp, enINSTRtoABUS_andtad, enINSTRtoABUS_dca, enINSTRtoABUS_ai, enINSTRtoABUS_dca, enINSTRtoABUS_isz, enINSTRtoABUS_jms);
  not not_11 (not_11_out, or_7_out);
  _74ls374 _74ls374_3 (
    .Q0(ABUS[0]), .Q1(ABUS[1]), .Q2(ABUS[2]), .Q3(ABUS[3]), .Q4(ABUS[4]), .Q5(ABUS[5]), .Q6(ABUS[6]),
    .Q7(ABUS[7]), .nOC(not_11_out), .CLK(or_8_out), .D0(DAW[0]), .D1(DAW[1]), .D2(DAW[2]), .D3(DAW[3]),
    .D4(DAW[4]), .D5(DAW[5]), .D6(DAW[6]), .D7(DAW[7]));  // open: iv
  _74ls374 _74ls374_4 (
    .Q0(ABUS[8]), .Q1(ABUS[9]), .Q2(ABUS[10]), .Q3(ABUS[11]), .nOC(not_11_out), .CLK(or_8_out), .D0(DAW[8]),
    .D1(DAW[9]), .D2(DAW[10]), .D3(DAW[11]), .D4(1'b0), .D5(1'b0), .D6(1'b0), .D7(1'b0));  // open: Q4, Q5, Q6, Q7, iv
  // Probe on ramspy_1_o
  LED led_73 (.in(L_OPR3[0]));
  Seven_Seg_Hex seven_seg_hex_4 (.d({1'b0, IRA[11:9]}), .dp(1'b0));
  Seven_Seg_Hex seven_seg_hex_5 (.d({1'b0, IR[11:9]}), .dp(1'b0));
  Seven_Seg_Hex seven_seg_hex_6 (.d({1'b0, ACC[11:9]}), .dp(1'b0));
  LED led_74 (.in(LINK));
  Seven_Seg_Hex seven_seg_hex_7 (.d({1'b0, MQ[11:9]}), .dp(1'b0));
  and and_3 (and_3_out, PC[7], isCurrPage);
  and and_4 (and_4_out, PC[8], isCurrPage);
  and and_5 (and_5_out, PC[9], isCurrPage);
  and and_6 (and_6_out, PC[10], isCurrPage);
  and and_7 (and_7_out, PC[11], isCurrPage);
  Seven_Seg_Hex seven_seg_hex_8 (.d({1'b0, IRA[8:6]}), .dp(1'b0));
  Seven_Seg_Hex seven_seg_hex_9 (.d({1'b0, IR[8:6]}), .dp(1'b0));
  Seven_Seg_Hex seven_seg_hex_10 (.d({1'b0, ACC[8:6]}), .dp(1'b0));
  Seven_Seg_Hex seven_seg_hex_11 (.d({1'b0, MQ[8:6]}), .dp(1'b0));
  not not_12 (not_12_out, or_9_out);
  Seven_Seg_Hex seven_seg_hex_12 (.d({1'b0, IRA[5:3]}), .dp(1'b0));
  Seven_Seg_Hex seven_seg_hex_13 (.d({1'b0, IR[5:3]}), .dp(1'b0));
  Seven_Seg_Hex seven_seg_hex_14 (.d({1'b0, ACC[5:3]}), .dp(1'b0));
  Seven_Seg_Hex seven_seg_hex_15 (.d({1'b0, MQ[5:3]}), .dp(1'b0));
  _74LS244 _74ls244_1 (
    ._1A1(IR[0]), ._1A2(IR[1]), ._1A3(IR[2]), ._1A4(IR[3]), ._1nG(not_12_out), ._2A1(IR[4]), ._2A2(IR[5]),
    ._2A3(IR[6]), ._2A4(and_3_out), ._2nG(not_12_out), ._1Y1(ABUS[0]), ._1Y2(ABUS[1]), ._1Y3(ABUS[2]),
    ._1Y4(ABUS[3]), ._2Y1(ABUS[4]), ._2Y2(ABUS[5]), ._2Y3(ABUS[6]), ._2Y4(ABUS[7]));
  _74LS244 _74ls244_2 (
    ._1A1(and_4_out), ._1A2(and_5_out), ._1A3(and_6_out), ._1A4(and_7_out), ._1nG(not_12_out), ._2A1(1'b1),
    ._2A2(1'b1), ._2A3(1'b1), ._2A4(1'b1), ._2nG(1'b1), ._1Y1(ABUS[8]), ._1Y2(ABUS[9]), ._1Y3(ABUS[10]),
    ._1Y4(ABUS[11]));  // open: _2Y1, _2Y2, _2Y3, _2Y4
  Seven_Seg_Hex seven_seg_hex_16 (.d({1'b0, IRA[2:0]}), .dp(1'b0));
  Seven_Seg_Hex seven_seg_hex_17 (.d({1'b0, IR[2:0]}), .dp(1'b0));
  Seven_Seg_Hex seven_seg_hex_18 (.d({1'b0, ACC[2:0]}), .dp(1'b0));
  Seven_Seg_Hex seven_seg_hex_19 (.d({1'b0, MQ[2:0]}), .dp(1'b0));
  PullDown pulldown_4 (.out(L_GEN[3]));
  Seven_Seg_Hex seven_seg_hex_20 (.d({1'b0, ABUS[11:9]}), .dp(1'b0));
  Seven_Seg_Hex seven_seg_hex_21 (.d({1'b0, DAW[11:9]}), .dp(1'b0));
  Seven_Seg_Hex seven_seg_hex_22 (.d({1'b0, OBUS[11:9]}), .dp(1'b0));
  Seven_Seg_Hex seven_seg_hex_23 (.d({1'b0, SWITCH[11:9]}), .dp(1'b0));
  PullDown pulldown_5 (.out(L_OPR1[10]));
  Seven_Seg_Hex seven_seg_hex_24 (.d({1'b0, ABUS[8:6]}), .dp(1'b0));
  Seven_Seg_Hex seven_seg_hex_25 (.d({1'b0, DAW[8:6]}), .dp(1'b0));
  Seven_Seg_Hex seven_seg_hex_26 (.d({1'b0, OBUS[8:6]}), .dp(1'b0));
  Seven_Seg_Hex seven_seg_hex_27 (.d({1'b0, SWITCH[8:6]}), .dp(1'b0));
  Seven_Seg_Hex seven_seg_hex_28 (.d({1'b0, ABUS[5:3]}), .dp(1'b0));
  Seven_Seg_Hex seven_seg_hex_29 (.d({1'b0, DAW[5:3]}), .dp(1'b0));
  Seven_Seg_Hex seven_seg_hex_30 (.d({1'b0, OBUS[5:3]}), .dp(1'b0));
  Seven_Seg_Hex seven_seg_hex_31 (.d({1'b0, SWITCH[5:3]}), .dp(1'b0));
  Seven_Seg_Hex seven_seg_hex_32 (.d({1'b0, ABUS[2:0]}), .dp(1'b0));
  Seven_Seg_Hex seven_seg_hex_33 (.d({1'b0, DAW[2:0]}), .dp(1'b0));
  Seven_Seg_Hex seven_seg_hex_34 (.d({1'b0, OBUS[2:0]}), .dp(1'b0));
  Seven_Seg_Hex seven_seg_hex_35 (.d({1'b0, SWITCH[2:0]}), .dp(1'b0));
  PullDown pulldown_6 (.out(L_OPR3[0]));
  PullDown pulldown_7 (.out(L_OPR3[1]));
  PullDown pulldown_8 (.out(L_OPR3[2]));
  PullDown pulldown_9 (.out(L_OPR3[3]));
  PullDown pulldown_10 (.out(L_OPR3[4]));
  PullDown pulldown_11 (.out(L_OPR3[5]));
  PullDown pulldown_12 (.out(L_OPR3[6]));
  PullDown pulldown_13 (.out(L_OPR3[12]));
  or or_10 (or_10_out, enACCtoDBUS_dca, enACCtoDBUS_2);
  or or_11 (or_11_out, enACCclear_dca, enACCclear_mop3a, CAF_6007, enACCclear_iot1);
  // Probe on ALU_out
  or or_12 (or_12_out, ckACC_mop1, ckACC_2, ckACC_mop2, ckACC_gtf, ckACC_4, ckACC_5, ckACC_iot1);
  or or_13 (or_13_out, CAF_6007, RTF_linkClr);
  or or_14 (or_14_out, ckIncPC_LoadIR, ckIncPC_jms1, ckIncPC_irq1, 1'b0, 1'b0, not_17_out);
  or or_15 (or_15_out, ckSetPC_0, ckSetPC_jmp, ckSetPC_jms, 1'b0, 1'b0, 1'b0);
  or or_16 (or_16_out, enPCtoABUS_0, enPCtoABUS_LoadIR, enPCtoABUS_mop2, enPCtoABUS_irq);
  or or_17 (or_17_out, ckIncPC_jms1, enPCtoDBUS_irq, 1'b0, 1'b0);
  not not_13 (not_13_out, or_10_out);
  not not_14 (not_14_out, or_11_out);
  not not_15 (not_15_out, RTF_linkSet);
  not not_16 (not_16_out, or_13_out);
  not not_17 (not_17_out, not_18_out);
  not not_18 (not_18_out, or_15_out);
  not not_19 (not_19_out, or_16_out);
  not not_20 (not_20_out, or_17_out);
  _74LS273 _74ls273_5 (
    .CP(or_12_out), .nMR(not_14_out), .D0(ALU_out[0]), .D1(ALU_out[1]), .D2(ALU_out[2]), .D3(ALU_out[3]),
    .D4(ALU_out[4]), .D5(ALU_out[5]), .D6(ALU_out[6]), .D7(ALU_out[7]), .Q0(ACC[0]), .Q1(ACC[1]),
    .Q2(ACC[2]), .Q3(ACC[3]), .Q4(ACC[4]), .Q5(ACC[5]), .Q6(ACC[6]), .Q7(ACC[7]));
  _74LS273 _74ls273_6 (
    .CP(or_12_out), .nMR(not_14_out), .D0(ALU_out[8]), .D1(ALU_out[9]), .D2(ALU_out[10]), .D3(ALU_out[11]),
    .D4(1'b0), .D5(1'b0), .D6(1'b0), .D7(1'b0), .Q0(ACC[8]), .Q1(ACC[9]), .Q2(ACC[10]), .Q3(ACC[11]));  // open: Q4, Q5, Q6, Q7
  _74LS74 _74ls74_1 (
    ._1nSD(not_15_out), ._1D(ALU_Lout), ._1CP(or_12_out), ._1nRD(not_16_out), ._2nSD(1'b1), ._2D(1'b1),
    ._2CP(1'b1), ._2nRD(1'b1), ._1Q(LINK));  // open: _1nQ, _2Q, _2nQ
  PullDown pulldown_14 (.out(ABUS[2]));
  PullDown pulldown_15 (.out(ABUS[3]));
  PullDown pulldown_16 (.out(ABUS[6]));
  PullDown pulldown_17 (.out(ABUS[10]));
  PullDown pulldown_18 (.out(ABUS[11]));
  not not_21 (not_21_out, clrPC_irq);
  D_FF d_ff_2 (.D(1'b1), .C(_25Hz), .Q(d_ff_2_q));  // open: nQ
  Button R (.out(R_out));
  Button H (.out(H_out));
  Button S (.out(S_out));
  Button T (.out(T_out));
  Button M (.out(M_out));
  or or_18 (or_18_out, ACC[0], ACC[1], ACC[2], ACC[3], ACC[4], ACC[5], ACC[6], ACC[7], ACC[8], ACC[9], ACC[10], ACC[11]);
  not not_22 (not_22_out, CLL);
  PullDown pulldown_19 (.out(ABUS[1]));
  PullDown pulldown_20 (.out(ABUS[0]));
  PullDown pulldown_21 (.out(ABUS[5]));
  PullDown pulldown_22 (.out(ABUS[4]));
  assign ABUS[7] = ckSetPC_0 ? 1'b1 : 1'bz;  // Driver driver_1
  PullDown pulldown_23 (.out(ABUS[9]));
  PullDown pulldown_24 (.out(ABUS[8]));
  not not_23 (fAccZero, or_18_out);
  and and_8 (and_8_out, LINK, not_22_out);
  not not_24 (not_24_out, enALUor_mop2);
  D_FF d_ff_3 (.D(d_ff_2_q), .C(_25Hz), .nQ(d_ff_3_nq));  // open: Q
  or or_19 (or_19_out, H_out, BP, STOP);
  and and_9 (and_9_out, T_out, _25Hz);
  xor xor_1 (xor_1_out, and_8_out, CML);
  _74LS161 _74ls161_1 (
    .CLK(or_14_out), .A(ABUS[0]), .B(ABUS[1]), .C(ABUS[2]), .D(ABUS[3]), .nLD(not_18_out), .nCLR(not_21_out),
    .ENT(1'b1), .ENP(1'b1), .QA(PC[0]), .QB(PC[1]), .QC(PC[2]), .QD(PC[3]), .RCO(_74ls161_1_rco));
  _74LS161 _74ls161_2 (
    .CLK(or_14_out), .A(ABUS[4]), .B(ABUS[5]), .C(ABUS[6]), .D(ABUS[7]), .nLD(not_18_out), .nCLR(not_21_out),
    .ENT(_74ls161_1_rco), .ENP(_74ls161_1_rco), .QA(PC[4]), .QB(PC[5]), .QC(PC[6]), .QD(PC[7]),
    .RCO(_74ls161_2_rco));
  _74LS161 _74ls161_3 (
    .CLK(or_14_out), .A(ABUS[8]), .B(ABUS[9]), .C(ABUS[10]), .D(ABUS[11]), .nLD(not_18_out),
    .nCLR(not_21_out), .ENT(_74ls161_2_rco), .ENP(_74ls161_2_rco), .QA(PC[8]), .QB(PC[9]), .QC(PC[10]),
    .QD(PC[11]));  // open: RCO
  and and_10 (RESET, d_ff_2_q, d_ff_3_nq);
  or or_20 (or_20_out, S_out, and_9_out);
  _74LS541 _74ls541_1 (
    .nOE1(not_13_out), .nOE2(not_13_out), ._0D(ACC[0]), ._1D(ACC[1]), ._2D(ACC[2]), ._3D(ACC[3]),
    ._4D(ACC[4]), ._5D(ACC[5]), ._6D(ACC[6]), ._7D(ACC[7]), ._0O(DAW[0]), ._1O(DAW[1]), ._2O(DAW[2]),
    ._3O(DAW[3]), ._4O(DAW[4]), ._5O(DAW[5]), ._6O(DAW[6]), ._7O(DAW[7]));
  _74LS541 _74ls541_2 (
    .nOE1(not_13_out), .nOE2(not_13_out), ._0D(ACC[8]), ._1D(ACC[9]), ._2D(ACC[10]), ._3D(ACC[11]),
    ._4D(1'b0), ._5D(1'b0), ._6D(1'b0), ._7D(1'b0), ._0O(DAW[8]), ._1O(DAW[9]), ._2O(DAW[10]), ._3O(DAW[11]));  // open: _4O, _5O, _6O, _7O
  xor xor_2 (ALU_Lin, xor_1_out, IAC_carryout);
  _74LS244 _74ls244_3 (
    ._1A1(SWITCH[0]), ._1A2(SWITCH[1]), ._1A3(SWITCH[2]), ._1A4(SWITCH[3]), ._1nG(not_24_out),
    ._2A1(SWITCH[4]), ._2A2(SWITCH[5]), ._2A3(SWITCH[6]), ._2A4(SWITCH[7]), ._2nG(not_24_out),
    ._1Y1(OBUS[0]), ._1Y2(OBUS[1]), ._1Y3(OBUS[2]), ._1Y4(OBUS[3]), ._2Y1(OBUS[4]), ._2Y2(OBUS[5]),
    ._2Y3(OBUS[6]), ._2Y4(OBUS[7]));
  _74LS244 _74ls244_4 (
    ._1A1(SWITCH[8]), ._1A2(SWITCH[9]), ._1A3(SWITCH[10]), ._1A4(SWITCH[11]), ._1nG(not_24_out), ._2A1(1'b1),
    ._2A2(1'b1), ._2A3(1'b1), ._2A4(1'b1), ._2nG(1'b1), ._1Y1(OBUS[8]), ._1Y2(OBUS[9]), ._1Y3(OBUS[10]),
    ._1Y4(OBUS[11]));  // open: _2Y1, _2Y2, _2Y3, _2Y4
  or or_21 (ckSetPC_0, RESET, _2_out);
  Button _2 (.out(_2_out));
  OneShot oneshot_2 (.i(R_out), .o(oneshot_2_o));
  OneShot oneshot_3 (.i(or_19_out), .o(oneshot_3_o));
  OneShot oneshot_4 (.i(or_20_out), .o(oneshot_4_o));
  // Probe PC on PC
  Delay #(.delayTime(5)) delay_1 (.in(ckSetPC_0), .out(enPCtoABUS_0));
  Delay #(.delayTime(10)) delay_2 (.in(ckSetPC_0), .out(ckIR_0));
  not not_25 (not_25_out, oneshot_2_o);
  not not_26 (not_26_out, oneshot_3_o);
  not not_27 (not_27_out, oneshot_4_o);
  not not_28 (not_28_out, iDone);
  // Probe on ACC
  // Probe on DAW[11:0]
  _74LS244 _74ls244_5 (
    ._1A1(PC[0]), ._1A2(PC[1]), ._1A3(PC[2]), ._1A4(PC[3]), ._1nG(not_19_out), ._2A1(PC[4]), ._2A2(PC[5]),
    ._2A3(PC[6]), ._2A4(PC[7]), ._2nG(not_19_out), ._1Y1(ABUS[0]), ._1Y2(ABUS[1]), ._1Y3(ABUS[2]),
    ._1Y4(ABUS[3]), ._2Y1(ABUS[4]), ._2Y2(ABUS[5]), ._2Y3(ABUS[6]), ._2Y4(ABUS[7]));
  _74LS244 _74ls244_6 (
    ._1A1(PC[8]), ._1A2(PC[9]), ._1A3(PC[10]), ._1A4(PC[11]), ._1nG(not_19_out), ._2A1(1'b1), ._2A2(1'b1),
    ._2A3(1'b1), ._2A4(1'b1), ._2nG(1'b1), ._1Y1(ABUS[8]), ._1Y2(ABUS[9]), ._1Y3(ABUS[10]), ._1Y4(ABUS[11]));  // open: _2Y1, _2Y2, _2Y3, _2Y4
  _74LS244 _74ls244_7 (
    ._1A1(PC[0]), ._1A2(PC[1]), ._1A3(PC[2]), ._1A4(PC[3]), ._1nG(not_20_out), ._2A1(PC[4]), ._2A2(PC[5]),
    ._2A3(PC[6]), ._2A4(PC[7]), ._2nG(not_20_out), ._1Y1(DAW[0]), ._1Y2(DAW[1]), ._1Y3(DAW[2]),
    ._1Y4(DAW[3]), ._2Y1(DAW[4]), ._2Y2(DAW[5]), ._2Y3(DAW[6]), ._2Y4(DAW[7]));
  _74LS244 _74ls244_8 (
    ._1A1(PC[8]), ._1A2(PC[9]), ._1A3(PC[10]), ._1A4(PC[11]), ._1nG(not_20_out), ._2A1(1'b1), ._2A2(1'b1),
    ._2A3(1'b1), ._2A4(1'b1), ._2nG(1'b1), ._1Y1(DAW[8]), ._1Y2(DAW[9]), ._1Y3(DAW[10]), ._1Y4(DAW[11]));  // open: _2Y1, _2Y2, _2Y3, _2Y4
  _74LS74 _74ls74_2 (
    ._1nSD(not_25_out), ._1D(1'b0), ._1CP(RESET), ._1nRD(not_26_out), ._2nSD(not_27_out), ._2D(1'b0),
    ._2CP(RESET), ._2nRD(not_28_out), ._1Q(_74ls74_2__1q), ._1nQ(_74ls74_2__1nq), ._2Q(_74ls74_2__2q));  // open: _2nQ
  or or_22 (or_22_out, ckMQ_1, ckACC_5);
  OneShot oneshot_5 (.i(_74ls74_2__1q), .o(oneshot_5_o));
  not not_29 (not_29_out, CLA_4);
  // Probe on ACC
  or or_23 (or_23_out, enACCtoDBUS_2, CLA_4);
  or or_24 (or_24_out, oneshot_4_o, oneshot_5_o);
  or or_25 (or_25_out, _74ls74_2__1nq, _74ls74_2__2q);
  and and_11 (and_11_out, or_25_out, iDone);
  _74LS273 _74ls273_7 (
    .CP(or_22_out), .nMR(1'b1), .D0(ACC[0]), .D1(ACC[1]), .D2(ACC[2]), .D3(ACC[3]), .D4(ACC[4]), .D5(ACC[5]),
    .D6(ACC[6]), .D7(ACC[7]), .Q0(_74ls273_7_q0), .Q1(_74ls273_7_q1), .Q2(_74ls273_7_q2), .Q3(_74ls273_7_q3),
    .Q4(_74ls273_7_q4), .Q5(_74ls273_7_q5), .Q6(_74ls273_7_q6), .Q7(_74ls273_7_q7));
  _74LS273 _74ls273_8 (
    .CP(or_22_out), .nMR(1'b1), .D0(ACC[8]), .D1(ACC[9]), .D2(ACC[10]), .D3(ACC[11]), .D4(1'b0), .D5(1'b0),
    .D6(1'b0), .D7(1'b0), .Q0(_74ls273_8_q0), .Q1(_74ls273_8_q1), .Q2(_74ls273_8_q2), .Q3(_74ls273_8_q3));  // open: Q4, Q5, Q6, Q7
  not not_30 (not_30_out, or_23_out);
  not not_31 (not_31_out, or_24_out);
  OneShot oneshot_6 (.i(and_11_out), .o(oneshot_6_o));
  not not_32 (not_32_out, oneshot_6_o);
  _74LS373 _74ls373_1 (
    .Q0(MQ[0]), .Q1(MQ[1]), .Q2(MQ[2]), .Q3(MQ[3]), .Q4(MQ[4]), .Q5(MQ[5]), .Q6(MQ[6]), .Q7(MQ[7]),
    .nOC(1'b0), .C(not_29_out), .D0(_74ls273_7_q0), .D1(_74ls273_7_q1), .D2(_74ls273_7_q2),
    .D3(_74ls273_7_q3), .D4(_74ls273_7_q4), .D5(_74ls273_7_q5), .D6(_74ls273_7_q6), .D7(_74ls273_7_q7));
  _74LS373 _74ls373_2 (
    .Q0(MQ[8]), .Q1(MQ[9]), .Q2(MQ[10]), .Q3(MQ[11]), .nOC(1'b0), .C(not_29_out), .D0(_74ls273_8_q0),
    .D1(_74ls273_8_q1), .D2(_74ls273_8_q2), .D3(_74ls273_8_q3), .D4(1'b0), .D5(1'b0), .D6(1'b0), .D7(1'b0));  // open: Q4, Q5, Q6, Q7
  _74LS238 _74ls238_1 (
    .A(IR[9]), .B(IR[10]), .C(IR[11]), .G(1'b1), .nGB(1'b0), .nGA(inhibitIR), .Y0(AND), .Y1(L_GEN[10]),
    .Y2(ISZ), .Y3(DCA), .Y4(JMS), .Y5(JMP), .Y6(IOT), .Y7(L_GEN[4]));
  not not_33 (not_33_out, IR[0]);
  not not_34 (not_34_out, IR[8]);
  _74LS238 _74ls238_2 (
    .A(IR[3]), .B(IR[4]), .C(IR[5]), .G(IOT), .nGB(1'b0), .nGA(1'b0), .Y0(IOT_CPU), .Y1(IOT_HISPEEDREADER),
    .Y2(IOT_HISPEEDPUNCH), .Y3(IOT_TTYREADER), .Y4(IOT_TTYPUNCH));  // open: Y5, Y6, Y7
  _74LS238 _74ls238_3 (
    .A(IR[0]), .B(IR[1]), .C(IR[2]), .G(IOT_CPU), .nGB(1'b0), .nGA(1'b0), .Y0(L_CPU[7]), .Y1(ION_6001),
    .Y2(IOF_6002), .Y3(L_CPU[4]), .Y4(GTF_6004), .Y5(L_CPU[2]), .Y6(L_CPU[1]), .Y7(CAF_6007));
  _74LS238 _74ls238_4 (
    .A(IR[0]), .B(IR[1]), .C(IR[2]), .G(IOT_TTYREADER), .nGB(1'b0), .nGA(1'b0), .Y0(KCF_6030), .Y1(KSF_6031),
    .Y2(KCC_6032), .Y4(KRS_6034), .Y5(KIE_6035), .Y6(KRB_6036));  // open: Y3, Y7
  _74LS238 _74ls238_5 (
    .A(IR[0]), .B(IR[1]), .C(IR[2]), .G(IOT_TTYPUNCH), .nGB(1'b0), .nGA(1'b0), .Y0(L_PRN[5]), .Y1(L_PRN[4]),
    .Y2(L_PRN[3]), .Y4(L_PRN[2]), .Y5(L_PRN[1]), .Y6(L_PRN[0]));  // open: Y3, Y7
  _74LS74 _74ls74_3 (
    ._1nSD(not_31_out), ._1D(1'b0), ._1CP(RESET), ._1nRD(not_32_out), ._2nSD(1'b1), ._2D(_74ls74_3__1q),
    ._2CP(MAX), ._2nRD(1'b1), ._1Q(_74ls74_3__1q), ._2Q(_74ls74_3__2q));  // open: _1nQ, _2nQ
  and and_12 (MOP3, IR[0], IR[8], L_GEN[4]);
  and and_13 (MOP2, not_33_out, IR[8], L_GEN[4]);
  and and_14 (MOP1, not_34_out, L_GEN[4]);
  nor nor_1 (nor_1_out, IOT, L_GEN[4]);
  and and_15 (and_15_out, _74ls74_3__2q, MAX);
  and and_16 (ZEROPAGE, IR[7], nor_1_out);
  and and_17 (INDIRECT, IR[8], nor_1_out);
  _74LS541 _74ls541_3 (
    .nOE1(not_30_out), .nOE2(not_30_out), ._0D(MQ[0]), ._1D(MQ[1]), ._2D(MQ[2]), ._3D(MQ[3]), ._4D(MQ[4]),
    ._5D(MQ[5]), ._6D(MQ[6]), ._7D(MQ[7]), ._0O(OBUS[0]), ._1O(OBUS[1]), ._2O(OBUS[2]), ._3O(OBUS[3]),
    ._4O(OBUS[4]), ._5O(OBUS[5]), ._6O(OBUS[6]), ._7O(OBUS[7]));
  _74LS541 _74ls541_4 (
    .nOE1(not_30_out), .nOE2(not_30_out), ._0D(MQ[8]), ._1D(MQ[9]), ._2D(MQ[10]), ._3D(MQ[11]), ._4D(1'b0),
    ._5D(1'b0), ._6D(1'b0), ._7D(1'b0), ._0O(OBUS[8]), ._1O(OBUS[9]), ._2O(OBUS[10]), ._3O(OBUS[11]));  // open: _4O, _5O, _6O, _7O
  or or_26 (CLK_t, and_15_out, M_out);
  // Probe on AND
  // Probe on L_GEN[10]
  // Probe on ISZ
  // Probe on DCA
  // Probe on JMS
  // Probe on JMP
  // Probe on IOT
  // Probe on L_GEN[4]
  // Probe on OBUS
  or or_27 (or_27_out, AND, L_GEN[10], DCA, JMP, JMS);
  or or_28 (ii, ii_mop1, ckACC_2, ii_jmp, ii_dca, ii_iot, ii_isz, ii_mop2, ii_jms, ii_mop3a);
  or or_29 (iDone, iDone1, ckIRQhandler);
  or or_30 (INC1, ii_dca, ckACC_2, ckACC_mop1, INC1_mop2, ckSetPC_jms, INC1_mop3a, INC1_iot, INC1_isz);
  or or_31 (INC2, INC2_mop2, INC2_isz, INC2_iot3, INC2_iot5, INC2_iot1, INC2_iot2, INC2_iot4);
  or or_32 (or_32_out, AND, L_GEN[10]);
  RS_FF_AS rs_ff_as_1 (.S(ii), .R(iDone), .Q(inhibitIR));  // open: nQ
  // Probe on iDone
  SequencerAI sequencerai_1 (
    .EN(or_27_out), .CLK(CLK_t), .fAI(fAutoinc), .DONE(ii), .P1a(enRAMtoDBUS_ai), .P1b(enINSTRtoABUS_ai),
    .P2(ckIncDBUS__ai), .P3a(weRAM_ai), .P3b(enIncToDBUS_ai), .Fin(aiFinished));
  and and_18 (and_18_out, aiFinished, or_32_out);
  and and_19 (and_19_out, aiFinished, DCA);
  and and_20 (and_20_out, aiFinished, JMP);
  and and_21 (and_21_out, aiFinished, JMS);
  Sequencer AND_TAD (
    .EN(and_18_out), .CLK(CLK_t), .DONE(ckACC_2), .D1(enRAMtoDBUS_andtad), .P1(AND_TAD_p1), .P2(AND_TAD_p2),
    .D3(AND_TAD_d3), .P3(AND_TAD_p3), .D4(AND_TAD_d4), .P4(AND_TAD_p4), .D5(AND_TAD_d5), .P5(AND_TAD_p5),
    .D6(AND_TAD_d6), .P6(AND_TAD_p6), .D7(enALUtoACC_andtad), .P7(AND_TAD_p7), .D8(ckACC_2));  // open: D2
  Sequencer u_DCA (
    .EN(and_19_out), .CLK(CLK_t), .DONE(ii_dca), .D1(DCA_d1), .P1(DCA_p1), .D2(DCA_d2), .P2(DCA_p2),
    .D3(DCA_d3), .P3(DCA_p3), .D4(DCA_d4), .P4(DCA_p4), .D5(DCA_d5), .P5(DCA_p5), .D6(enACCtoDBUS_dca),
    .P6(weRAM_dca), .D7(enACCclear_dca), .P7(DCA_p7), .D8(ii_dca));
  Sequencer JMP_JMPi (
    .EN(and_20_out), .CLK(CLK_t), .DONE(ii_jmp), .D1(enRAMtoDBUS_jmp), .P1(JMP_JMPi_p1), .D2(JMP_JMPi_d2),
    .P2(JMP_JMPi_p2), .D3(JMP_JMPi_d3), .P3(JMP_JMPi_p3), .D4(JMP_JMPi_d4), .P4(JMP_JMPi_p4),
    .D5(JMP_JMPi_d5), .P5(JMP_JMPi_p5), .D6(JMP_JMPi_d6), .P6(JMP_JMPi_p6), .D7(ckSetPC_jmp),
    .P7(JMP_JMPi_p7), .D8(ii_jmp));
  Sequencer JMS_JMSi (
    .EN(and_21_out), .CLK(CLK_t), .DONE(ii_jms), .D1(enRAMtoDBUS_jms), .P1(JMS_JMSi_p1), .D2(JMS_JMSi_d2),
    .P2(JMS_JMSi_p2), .D3(JMS_JMSi_d3), .P3(ckIncPC_jms1), .D4(JMS_JMSi_d4), .P4(ckSetPC_jms), .D5(ii_jms),
    .P5(JMS_JMSi_p5), .D6(JMS_JMSi_d6), .P6(JMS_JMSi_p6), .D7(JMS_JMSi_d7), .P7(JMS_JMSi_p7), .D8(JMS_JMSi_d8));
  Sequencer ISZ_ISZi (
    .EN(ISZ), .CLK(CLK_t), .DONE(ii_isz), .D1(ISZ_ISZi_d1), .P1(ISZ_ISZi_p1), .P2(ISZ_ISZi_p2),
    .P3(ISZ_ISZi_p3), .D4(ISZ_ISZi_d4), .P5(ckIncDBUS_isz1), .P6(enIncToDBUS_isz1), .P7(INC1_isz), .D8(ii_isz));  // open: D2, D3, P4, D5, D6, D7
  and and_22 (and_22_out, ~enIRQ, inhibitIR);  // And
  and and_23 (and_23_out, inhibitIR, enIRQ);
  Sequencer sequencer_1 (
    .EN(and_22_out), .CLK(CLK_t), .DONE(iDone1), .D1(enPCtoABUS_LoadIR), .P1(iDoneBeforeIRQ),
    .D2(sequencer_1_d2), .P2(ckIR_LoadIR), .D3(sequencer_1_d3), .P3(sequencer_1_p3), .D4(sequencer_1_d4),
    .P4(sequencer_1_p4), .D5(sequencer_1_d5), .P5(sequencer_1_p5), .D6(sequencer_1_d6), .P6(sequencer_1_p6),
    .D7(sequencer_1_d7), .P7(sequencer_1_p7), .D8(iDone1));
  Sequencer sequencer_2 (
    .EN(and_23_out), .CLK(CLK_t), .DONE(ckIRQhandler), .D1(sequencer_2_d1), .P1(weRAM_irq),
    .D2(sequencer_2_d2), .P2(sequencer_2_p2), .D3(sequencer_2_d3), .P3(clrPC_irq), .D4(enPCtoABUS_irq),
    .P4(sequencer_2_p4), .D5(sequencer_2_d5), .P5(ckIncPC_irq1), .D6(sequencer_2_d6), .P6(ckIR_irq),
    .D7(sequencer_2_d7), .P7(sequencer_2_p7), .D8(ckIRQhandler));
  and and_24 (and_24_out, JMP_JMPi_d2, ~fIndirect);  // And
  and and_25 (ckDBUStoABUS_jmp, JMP_JMPi_d2, fIndirect);
  or or_33 (or_33_out, enIncToDBUS_isz1, enIncToDBUS_isz2);
  or or_34 (or_34_out, sequencer_1_p3, weRAM_irq);
  and and_26 (and_26_out, enRAMtoDBUS_andtad, ~fIndirect);  // And
  and and_27 (enALUand, AND, enALUtoACC_andtad);
  and and_28 (enALUadd, L_GEN[10], enALUtoACC_andtad);
  and and_29 (and_29_out, DCA_d1, ~fIndirect);  // And
  or or_35 (enINSTRtoABUS_jmp, JMP_JMPi_p1, and_24_out);
  and and_30 (enRAMtoDBUS_isz, ISZ_ISZi_d1, ~or_33_out);  // And
  Delay #(.delayTime(20)) delay_3 (.in(iDoneBeforeIRQ), .out(delay_3_out));
  or or_36 (enINSTRtoABUS_andtad, and_26_out, AND_TAD_p1, AND_TAD_p2);
  and and_31 (ckDBUStoABUS_andtad, AND_TAD_p2, fIndirect);
  and and_32 (enDBUStoABUS_andtad, AND_TAD_d3, fIndirect);
  or or_37 (enRAMtoDBUS_dca, DCA_p1, DCA_p2, DCA_p3);
  or or_38 (enINSTRtoABUS_dca, and_29_out, DCA_p1, DCA_p2);
  and and_33 (ckDBUStoABUS_dca, DCA_p2, fIndirect);
  and and_34 (enDBUStoABUS_dca, DCA_d3, fIndirect);
  and and_35 (INC2_isz, INC1_isz, fDBUSisZero);
  OneShot oneshot_7 (.i(iDoneBeforeIRQ), .o(oneshot_7_o));
  OneShot oneshot_8 (.i(delay_3_out), .o(oneshot_8_o));
  RS_FF_AS rs_ff_as_2 (.S(INC1), .R(or_34_out), .Q(rs_ff_as_2_q));  // open: nQ
  RS_FF_AS rs_ff_as_3 (.S(INC2), .R(or_34_out), .Q(rs_ff_as_3_q));  // open: nQ
  and and_36 (and_36_out, JMS_JMSi_d2, ~fIndirect);  // And
  and and_37 (ckDBUStoABUS_jms, JMS_JMSi_d2, fIndirect);
  or or_39 (enPCtoDBUS_irq, weRAM_irq, sequencer_2_p2);
  or or_40 (enINSTRtoABUS_jms, JMS_JMSi_p1, and_36_out);
  and and_38 (and_38_out, ~fIndirect, ISZ_ISZi_d4);  // And
  and and_39 (ckDBUStoABUS_isz, ISZ_ISZi_d4, fIndirect);
  and and_40 (and_40_out, oneshot_7_o, rs_ff_as_2_q);
  and and_41 (and_41_out, oneshot_8_o, rs_ff_as_3_q);
  or or_41 (enINSTRtoABUS_isz, ISZ_ISZi_p1, ISZ_ISZi_p2, and_38_out, ISZ_ISZi_p3);
  and and_42 (ckIncDBUS__isz2, fAutoinc, ISZ_ISZi_p2);
  and and_43 (enIncToDBUS_isz2, fAutoinc, ISZ_ISZi_p3);
  or or_42 (ckIncPC_LoadIR, and_40_out, and_41_out);
  Sequencer u_MOP1 (
    .EN(MOP1), .CLK(CLK_t), .DONE(ii_mop1), .D1(enALUtoACC_mop1), .P1(MOP1_p1), .D2(ckACC_mop1),
    .P2(MOP1_p2), .D3(ii_mop1), .P3(MOP1_p3), .D4(MOP1_d4), .P4(MOP1_p4), .D5(MOP1_d5), .P5(MOP1_p5),
    .D6(MOP1_d6), .P6(MOP1_p6), .D7(MOP1_d7), .P7(MOP1_p7), .D8(MOP1_d8));
  Sequencer u_MOP2 (
    .EN(MOP2), .CLK(CLK_t), .DONE(ii_mop2), .D1(enPCtoABUS_mop2), .P1(MOP2_p1), .D2(MOP2_d2), .P2(INC1_mop2),
    .D3(enALUtoACC_mop2), .P3(MOP2_p3), .D4(MOP2_d4), .P4(MOP2_p4), .D5(MOP2_d5), .P5(MOP2_p5), .D6(ii_mop2),
    .P6(MOP2_p6), .D7(MOP2_d7), .P7(MOP2_p7), .D8(MOP2_d8));
  Sequencer u_MOP3 (
    .EN(MOP3), .CLK(CLK_t), .DONE(ii_mop3a), .D1(MOP3_d1), .P1(INC1_mop3a), .D2(MOP3_d2), .P2(MOP3_p2),
    .D3(MOP3_d3), .P3(MOP3_p3), .D4(ii_mop3a), .P4(MOP3_p4), .D5(MOP3_d5), .P5(MOP3_p5), .D6(MOP3_d6),
    .P6(MOP3_p6), .D7(MOP3_d7), .P7(MOP3_p7));  // open: D8
  not not_35 (not_35_out, IR[3]);
  not not_36 (not_36_out, IR[4]);
  not not_37 (not_37_out, IR[5]);
  not not_38 (not_38_out, IR[6]);
  and and_44 (IAC, MOP1, IR[0]);
  and and_45 (CML, MOP1, IR[4]);
  and and_46 (CMA, MOP1, IR[5]);
  and and_47 (CLL, MOP1, IR[6]);
  and and_48 (CLA_1, MOP1, IR[7]);
  or or_43 (or_43_out, L_OPR2[1], CLA_2);
  and and_49 (STOP, MOP2_d5, HLT);
  and and_50 (CODE_lsb, MOP3, IR[1]);
  and and_51 (CODE_mid, MOP3, IR[2]);
  and and_52 (CODE_msb, MOP3, IR[3]);
  and and_53 (MQL, MOP3, IR[4]);
  and and_54 (L_OPR3[10], MOP3, IR[5]);
  and and_55 (MQA, MOP3, IR[6]);
  and and_56 (CLA_3, MOP3, IR[7]);
  and and_57 (L_OPR3[9], MQA, MQL);
  _74LS238 _74ls238_6 (
    .A(IR[1]), .B(IR[2]), .C(IR[3]), .G(MOP1), .nGB(1'b0), .nGA(1'b0), .Y1(BSW), .Y2(L_OPR1[1]),
    .Y3(L_OPR1[2]), .Y4(L_OPR1[4]), .Y5(L_OPR1[3]));  // open: Y0, Y6, Y7
  and and_58 (HLT, MOP2, IR[1]);
  and and_59 (L_OPR2[1], MOP2, IR[2]);
  and and_60 (L_OPR2[2], MOP2, IR[3], IR[4]);
  and and_61 (L_OPR2[4], MOP2, IR[3], IR[5]);
  and and_62 (L_OPR2[5], MOP2, IR[3], IR[6]);
  and and_63 (L_OPR2[3], MOP2, not_35_out, IR[4]);
  and and_64 (L_OPR2[6], MOP2, not_35_out, IR[5]);
  and and_65 (L_OPR2[7], MOP2, not_35_out, IR[6]);
  and and_66 (CLA_2, MOP2, IR[7]);
  and and_67 (L_OPR2[8], MOP2, IR[3], not_36_out, not_37_out, not_38_out);
  and and_68 (INC2_mop2, INC1_mop2, fSkip);
  and and_69 (enALUor_mop2, enALUtoACC_mop2, L_OPR2[1]);
  and and_70 (ckACC_mop2, or_43_out, MOP2_p4);
  and and_71 (L_OPR3[7], MQL, ~MQA);  // And
  and and_72 (L_OPR3[8], ~MQL, MQA);  // And
  and and_73 (and_73_out, CLA, INC1_mop3a);
  and and_74 (ckMQ_1, MOP3_d2, L_OPR3[7]);
  and and_75 (and_75_out, L_OPR3[7], MOP3_p2);
  and and_76 (enACCtoDBUS_2, MOP3_d2, L_OPR3[8]);
  and and_77 (ckACC_4, L_OPR3[8], MOP3_p3);
  and and_78 (CLA_4, MOP3_d2, L_OPR3[9]);
  and and_79 (ckACC_5, L_OPR3[9], MOP3_p3);
  and and_80 (and_80_out, fAccZero, IR[5]);
  and and_81 (and_81_out, ACC[11], IR[6]);
  and and_82 (and_82_out, LINK, IR[4]);
  or or_44 (or_44_out, and_80_out, and_81_out, and_82_out);
  or or_45 (enACCclear_mop3a, and_73_out, and_75_out);
  xor xor_3 (fSkip, or_44_out, IR[3]);
  Sequencer u_IOT (
    .EN(IOT), .CLK(CLK_t), .DONE(ii_iot), .D1(IOT_d1), .P1(INC1_iot), .D2(IOT_d2), .P2(IOT_p2), .D3(ii_iot),
    .P3(IOT_p3), .D4(IOT_d4), .P4(IOT_p4), .D5(IOT_d5), .P5(IOT_p5), .D6(IOT_d6), .P6(IOT_p6), .D7(IOT_d7),
    .P7(IOT_p7), .D8(IOT_d8));
  // Probe on L_CPU[7]
  // Probe on ION_6001
  // Probe on IOF_6002
  // Probe on L_CPU[4]
  // Probe on GTF_6004
  // Probe on L_CPU[2]
  // Probe on L_CPU[1]
  // Probe on CAF_6007
  // Probe on L_PRN[5]
  // Probe on L_PRN[4]
  // Probe on L_PRN[3]
  // Probe on L_PRN[2]
  // Probe on L_PRN[1]
  // Probe on L_PRN[0]
  // Probe on KCF_6030
  // Probe on KSF_6031
  // Probe on KCC_6032
  // Probe on KIE_6035
  // Probe on KRB_6036
  or or_46 (or_46_out, INC2_iot5, IOF_6002);
  or or_47 (or_47_out, fPRN, fKBD);
  and and_83 (INC2_iot5, L_CPU[7], fGIE, INC1_iot);
  and and_84 (and_84_out, ION_6001, INC1_iot);
  and and_85 (and_85_out, or_46_out, INC1_iot);
  and and_86 (INC2_iot4, L_CPU[4], fPendInt, INC1_iot);
  and and_87 (and_87_out, INC1_iot, GTF_6004);
  and and_88 (and_88_out, INC1_iot, L_CPU[2]);
  and and_89 (and_89_out, INC1_iot, L_CPU[1]);
  and and_90 (CAF, INC1_iot, CAF_6007);
  and and_91 (and_91_out, L_PRN[5], INC1_iot);
  and and_92 (INC2_iot2, L_PRN[4], fPRN, INC1_iot);
  and and_93 (and_93_out, L_PRN[3], INC1_iot);
  and and_94 (and_94_out, INC1_iot, L_PRN[2]);
  and and_95 (INC2_iot1, L_PRN[1], or_47_out, INC1_iot);
  and and_96 (and_96_out, L_PRN[0], INC1_iot);
  and and_97 (and_97_out, KCF_6030, INC1_iot);
  and and_98 (INC2_iot3, KSF_6031, fKBD, INC1_iot);
  and and_99 (enACCclear_iot1, KCC_6032, INC1_iot);
  and and_100 (and_100_out, KRS_6034, INC1_iot);
  and and_101 (KIE, KIE_6035, INC1_iot);
  and and_102 (KRB, KRB_6036, INC1_iot);
  and and_103 (and_103_out, KRB_6036, IOT_p2);
  or or_48 (or_48_out, and_84_out, RTF_INTEset);
  or or_49 (or_49_out, RTF_INTEclr, ckIRQhandler, and_85_out, CAF);
  not not_39 (not_39_out, and_87_out);
  not not_40 (not_40_out, and_87_out);
  or or_50 (or_50_out, KRB, and_100_out);
  // Probe on PC
  // Probe on IRA
  // Probe on ACC
  // Probe on ABUS
  // Probe on DAW[11:0]
  not not_41 (not_41_out, not_40_out);
  not not_42 (not_42_out, not_41_out);
  or or_51 (or_51_out, and_94_out, and_96_out);
  // Probe on iDoneBeforeIRQ
  RS_FF_AS INTE (.S(or_48_out), .R(or_49_out), .Q(fGIE), .nQ(INTE_nq));
  not not_43 (not_43_out, not_42_out);
  not not_44 (not_44_out, or_50_out);
  not not_45 (not_45_out, not_44_out);
  D_FF_AS d_ff_as_1 (.Set(1'b0), .D(1'b1), .C(iDoneBeforeIRQ), .Clr(INTE_nq), .Q(d_ff_as_1_q));  // open: nQ
  not not_46 (not_46_out, not_43_out);
  not not_47 (ckACC_gtf, not_46_out);
  or or_52 (or_52_out, and_97_out, enACCclear_iot1, KRB, CAF);
  not not_48 (not_48_out, not_45_out);
  not not_49 (ckACC_iot1, not_48_out);
  D_FF_AS d_ff_as_2 (
    .Set(1'b0), .D(d_ff_as_1_q), .C(iDoneBeforeIRQ), .Clr(INTE_nq), .Q(d_ff_as_2_q), .nQ(d_ff_as_2_nq));
  and and_104 (RTF_linkSet, and_88_out, ACC[11]);
  and and_105 (RTF_linkClr, and_88_out, ~ACC[11]);  // And
  and and_106 (RTF_INTEclr, and_88_out, ACC[7]);
  and and_107 (RTF_INTEset, and_88_out, ~ACC[7]);  // And
  or or_53 (or_53_out, and_91_out, tty_1_txdone);
  or or_54 (or_54_out, and_93_out, CAF, and_96_out);
  RS_FF_AS PRN_FLAG (.S(or_53_out), .R(or_54_out), .Q(fPRN));  // open: nQ
  RS_FF_AS KBD_FLAG (.S(oneshot_9_o), .R(or_52_out), .Q(fKBD));  // open: nQ
  and and_108 (and_108_out, KIE, ACC[0]);
  and and_109 (and_109_out, KIE, ~ACC[0]);  // And
  and and_110 (enIRQ, d_ff_as_2_q, fPendInt, fGIE);
  and and_111 (fIrqDly, fGIE, d_ff_as_2_nq);
  // Probe on ACC
  or or_55 (or_55_out, CAF, and_108_out);
  RS_FF_AS TTY_IE (.S(or_55_out), .R(and_109_out), .Q(TTY_IE_q));  // open: nQ
  and and_112 (and_112_out, TTY_IE_q, fPRN);
  TTY tty_1 (
    .ck(clk), .Tx(ACC), .TxTrig(or_51_out), .RxAck(and_103_out), .RxEn(or_50_out), .TxDone(tty_1_txdone),
    .Rx(ALU_out), .RxAvail(tty_1_rxavail));
  _74LS244 _74ls244_9 (
    ._1A1(1'b0), ._1A2(1'b0), ._1A3(1'b0), ._1A4(1'b0), ._1nG(not_39_out), ._2A1(1'b0), ._2A2(1'b0),
    ._2A3(1'b0), ._2A4(fGIE), ._2nG(not_39_out), ._1Y1(ALU_out[0]), ._1Y2(ALU_out[1]), ._1Y3(ALU_out[2]),
    ._1Y4(ALU_out[3]), ._2Y1(ALU_out[4]), ._2Y2(ALU_out[5]), ._2Y3(ALU_out[6]), ._2Y4(ALU_out[7]));
  _74LS244 _74ls244_10 (
    ._1A1(1'b0), ._1A2(fPendInt), ._1A3(1'b0), ._1A4(LINK), ._1nG(not_39_out), ._2A1(LINK), ._2A2(1'b0),
    ._2A3(1'b0), ._2A4(1'b0), ._2nG(not_39_out), ._1Y1(ALU_out[8]), ._1Y2(ALU_out[9]), ._1Y3(ALU_out[10]),
    ._1Y4(ALU_out[11]), ._2Y1(ALU_Lout));  // open: _2Y2, _2Y3, _2Y4
  // Probe on ALU_out
  and and_113 (and_113_out, tty_1_rxavail, _25Hz);
  or or_56 (fPendInt, and_112_out, fKBD);
  OneShot oneshot_9 (.i(and_113_out), .o(oneshot_9_o));
  nor nor_2 (nor_2_out, CLA_1, CLA_2, CLA_3, CLA_4);
  not not_50 (not_50_out, enALUand);
  or or_57 (or_57_out, enALUor_mop2, enACCtoDBUS_2, CLA_4);
  not not_51 (CLA, nor_2_out);
  or or_58 (or_58_out, DAW[0], not_50_out);
  or or_59 (or_59_out, DAW[1], not_50_out);
  or or_60 (or_60_out, DAW[2], not_50_out);
  or or_61 (or_61_out, DAW[3], not_50_out);
  or or_62 (or_62_out, DAW[4], not_50_out);
  or or_63 (or_63_out, DAW[5], not_50_out);
  or or_64 (or_64_out, DAW[6], not_50_out);
  or or_65 (or_65_out, DAW[7], not_50_out);
  or or_66 (or_66_out, DAW[8], not_50_out);
  or or_67 (or_67_out, DAW[9], not_50_out);
  or or_68 (or_68_out, DAW[10], not_50_out);
  or or_69 (or_69_out, DAW[11], not_50_out);
  and and_114 (and_114_out[0], OBUS[0], or_57_out);
  and and_115 (and_114_out[1], OBUS[1], or_57_out);
  and and_116 (and_114_out[2], OBUS[2], or_57_out);
  and and_117 (and_114_out[3], OBUS[3], or_57_out);
  and and_118 (and_114_out[4], OBUS[4], or_57_out);
  and and_119 (and_114_out[5], OBUS[5], or_57_out);
  and and_120 (and_114_out[6], OBUS[6], or_57_out);
  and and_121 (and_114_out[7], OBUS[7], or_57_out);
  and and_122 (and_114_out[8], OBUS[8], or_57_out);
  and and_123 (and_114_out[9], OBUS[9], or_57_out);
  and and_124 (and_114_out[10], OBUS[10], or_57_out);
  and and_125 (and_114_out[11], OBUS[11], or_57_out);
  and and_126 (and_126_out[0], DAW[0], enALUadd);
  and and_127 (and_126_out[1], DAW[1], enALUadd);
  and and_128 (and_126_out[2], DAW[2], enALUadd);
  and and_129 (and_126_out[3], DAW[3], enALUadd);
  and and_130 (and_126_out[4], DAW[4], enALUadd);
  and and_131 (and_126_out[5], DAW[5], enALUadd);
  and and_132 (and_126_out[6], DAW[6], enALUadd);
  and and_133 (and_126_out[7], DAW[7], enALUadd);
  and and_134 (and_126_out[8], DAW[8], enALUadd);
  and and_135 (and_126_out[9], DAW[9], enALUadd);
  and and_136 (and_126_out[10], DAW[10], enALUadd);
  and and_137 (and_126_out[11], DAW[11], enALUadd);
  or or_70 (or_70_out, enALUtoACC_mop1, enALUtoACC_andtad, enALUtoACC_mop2, enACCtoDBUS_2, CLA_4);
  and and_138 (and_138_out, ACC[0], or_58_out, nor_2_out);
  and and_139 (and_139_out, ACC[1], or_59_out, nor_2_out);
  and and_140 (and_140_out, ACC[2], or_60_out, nor_2_out);
  and and_141 (and_141_out, ACC[3], or_61_out, nor_2_out);
  and and_142 (and_142_out, ACC[4], or_62_out, nor_2_out);
  and and_143 (and_143_out, ACC[5], or_63_out, nor_2_out);
  and and_144 (and_144_out, ACC[6], or_64_out, nor_2_out);
  and and_145 (and_145_out, ACC[7], or_65_out, nor_2_out);
  and and_146 (and_146_out, ACC[8], or_66_out, nor_2_out);
  and and_147 (and_147_out, ACC[9], or_67_out, nor_2_out);
  and and_148 (and_148_out, ACC[10], or_68_out, nor_2_out);
  and and_149 (and_149_out, ACC[11], or_69_out, nor_2_out);
  or or_71 (or_71_out, and_138_out, and_114_out[0]);
  or or_72 (or_72_out, and_139_out, and_114_out[1]);
  or or_73 (or_73_out, and_140_out, and_114_out[2]);
  or or_74 (or_74_out, and_141_out, and_114_out[3]);
  or or_75 (or_75_out, and_142_out, and_114_out[4]);
  or or_76 (or_76_out, and_143_out, and_114_out[5]);
  or or_77 (or_77_out, and_144_out, and_114_out[6]);
  or or_78 (or_78_out, and_145_out, and_114_out[7]);
  or or_79 (or_79_out, and_146_out, and_114_out[8]);
  or or_80 (or_80_out, and_147_out, and_114_out[9]);
  or or_81 (or_81_out, and_148_out, and_114_out[10]);
  or or_82 (or_82_out, and_149_out, and_114_out[11]);
  xor xor_4 (xor_4_out, CMA, or_71_out);
  xor xor_5 (xor_5_out, CMA, or_72_out);
  xor xor_6 (xor_6_out, CMA, or_73_out);
  xor xor_7 (xor_7_out, CMA, or_74_out);
  xor xor_8 (xor_8_out, CMA, or_75_out);
  xor xor_9 (xor_9_out, CMA, or_76_out);
  xor xor_10 (xor_10_out, CMA, or_77_out);
  xor xor_11 (xor_11_out, CMA, or_78_out);
  xor xor_12 (xor_12_out, CMA, or_79_out);
  xor xor_13 (xor_13_out, CMA, or_80_out);
  xor xor_14 (xor_14_out, CMA, or_81_out);
  xor xor_15 (xor_15_out, CMA, or_82_out);
  nand nand_1 (nand_1_out, BSW, or_70_out);
  nand nand_2 (nand_2_out, L_OPR1[1], or_70_out);
  nand nand_3 (nand_3_out, L_OPR1[2], or_70_out);
  _74LS283 _74ls283_4 (
    .A1(and_126_out[0]), .A2(and_126_out[1]), .A3(and_126_out[2]), .A4(and_126_out[3]), .B1(xor_4_out),
    .B2(xor_5_out), .B3(xor_6_out), .B4(xor_7_out), .S1(_74ls283_4_s1), .S2(_74ls283_4_s2),
    .S3(_74ls283_4_s3), .S4(_74ls283_4_s4), .C_in(IAC), .C_out(_74ls283_4_c_out));
  _74LS283 _74ls283_5 (
    .A1(and_126_out[4]), .A2(and_126_out[5]), .A3(and_126_out[6]), .A4(and_126_out[7]), .B1(xor_8_out),
    .B2(xor_9_out), .B3(xor_10_out), .B4(xor_11_out), .S1(_74ls283_5_s1), .S2(_74ls283_5_s2),
    .S3(_74ls283_5_s3), .S4(_74ls283_5_s4), .C_in(_74ls283_4_c_out), .C_out(_74ls283_5_c_out));
  _74LS283 _74ls283_6 (
    .A1(and_126_out[8]), .A2(and_126_out[9]), .A3(and_126_out[10]), .A4(and_126_out[11]), .B1(xor_12_out),
    .B2(xor_13_out), .B3(xor_14_out), .B4(xor_15_out), .S1(_74ls283_6_s1), .S2(_74ls283_6_s2),
    .S3(_74ls283_6_s3), .S4(_74ls283_6_s4), .C_in(_74ls283_5_c_out), .C_out(IAC_carryout));
  nand nand_4 (nand_4_out, L_OPR1[4], or_70_out);
  nand nand_5 (nand_5_out, L_OPR1[3], or_70_out);
  nand nand_6 (nand_6_out, or_70_out, and_150_out);
  and and_150 (and_150_out, nand_1_out, nand_2_out, nand_3_out, nand_4_out, nand_5_out);
  _74LS541 _74ls541_5 (
    .nOE1(nand_6_out), .nOE2(nand_6_out), ._0D(_74ls283_4_s1), ._1D(_74ls283_4_s2), ._2D(_74ls283_4_s3),
    ._3D(_74ls283_4_s4), ._4D(_74ls283_5_s1), ._5D(_74ls283_5_s2), ._6D(_74ls283_5_s3), ._7D(_74ls283_5_s4),
    ._0O(ALU_out[0]), ._1O(ALU_out[1]), ._2O(ALU_out[2]), ._3O(ALU_out[3]), ._4O(ALU_out[4]),
    ._5O(ALU_out[5]), ._6O(ALU_out[6]), ._7O(ALU_out[7]));
  _74LS541 _74ls541_6 (
    .nOE1(nand_6_out), .nOE2(nand_6_out), ._0D(_74ls283_6_s1), ._1D(_74ls283_6_s2), ._2D(_74ls283_6_s3),
    ._3D(_74ls283_6_s4), ._4D(1'b0), ._5D(1'b0), ._6D(1'b0), ._7D(ALU_Lin), ._0O(ALU_out[8]),
    ._1O(ALU_out[9]), ._2O(ALU_out[10]), ._3O(ALU_out[11]), ._7O(ALU_Lout));  // open: _4O, _5O, _6O
  _74LS541 _74ls541_7 (
    .nOE1(nand_1_out), .nOE2(nand_1_out), ._0D(_74ls283_5_s3), ._1D(_74ls283_5_s4), ._2D(_74ls283_6_s1),
    ._3D(_74ls283_6_s2), ._4D(_74ls283_6_s3), ._5D(_74ls283_6_s4), ._6D(_74ls283_4_s1), ._7D(_74ls283_4_s2),
    ._0O(ALU_out[0]), ._1O(ALU_out[1]), ._2O(ALU_out[2]), ._3O(ALU_out[3]), ._4O(ALU_out[4]),
    ._5O(ALU_out[5]), ._6O(ALU_out[6]), ._7O(ALU_out[7]));
  _74LS541 _74ls541_8 (
    .nOE1(nand_1_out), .nOE2(nand_1_out), ._0D(_74ls283_4_s3), ._1D(_74ls283_4_s4), ._2D(_74ls283_5_s1),
    ._3D(_74ls283_5_s2), ._4D(1'b0), ._5D(1'b0), ._6D(1'b0), ._7D(ALU_Lin), ._0O(ALU_out[8]),
    ._1O(ALU_out[9]), ._2O(ALU_out[10]), ._3O(ALU_out[11]), ._7O(ALU_Lout));  // open: _4O, _5O, _6O
  _74LS541 _74ls541_9 (
    .nOE1(nand_2_out), .nOE2(nand_2_out), ._0D(ALU_Lin), ._1D(_74ls283_4_s1), ._2D(_74ls283_4_s2),
    ._3D(_74ls283_4_s3), ._4D(_74ls283_4_s4), ._5D(_74ls283_5_s1), ._6D(_74ls283_5_s2), ._7D(_74ls283_5_s3),
    ._0O(ALU_out[0]), ._1O(ALU_out[1]), ._2O(ALU_out[2]), ._3O(ALU_out[3]), ._4O(ALU_out[4]),
    ._5O(ALU_out[5]), ._6O(ALU_out[6]), ._7O(ALU_out[7]));
  _74LS541 _74ls541_10 (
    .nOE1(nand_2_out), .nOE2(nand_2_out), ._0D(_74ls283_5_s4), ._1D(_74ls283_6_s1), ._2D(_74ls283_6_s2),
    ._3D(_74ls283_6_s3), ._4D(1'b0), ._5D(1'b0), ._6D(1'b0), ._7D(_74ls283_6_s4), ._0O(ALU_out[8]),
    ._1O(ALU_out[9]), ._2O(ALU_out[10]), ._3O(ALU_out[11]), ._7O(ALU_Lout));  // open: _4O, _5O, _6O
  _74LS541 _74ls541_11 (
    .nOE1(nand_3_out), .nOE2(nand_3_out), ._0D(_74ls283_6_s4), ._1D(ALU_Lin), ._2D(_74ls283_4_s1),
    ._3D(_74ls283_4_s2), ._4D(_74ls283_4_s3), ._5D(_74ls283_4_s4), ._6D(_74ls283_5_s1), ._7D(_74ls283_5_s2),
    ._0O(ALU_out[0]), ._1O(ALU_out[1]), ._2O(ALU_out[2]), ._3O(ALU_out[3]), ._4O(ALU_out[4]),
    ._5O(ALU_out[5]), ._6O(ALU_out[6]), ._7O(ALU_out[7]));
  _74LS541 _74ls541_12 (
    .nOE1(nand_3_out), .nOE2(nand_3_out), ._0D(_74ls283_5_s3), ._1D(_74ls283_5_s4), ._2D(_74ls283_6_s1),
    ._3D(_74ls283_6_s2), ._4D(1'b0), ._5D(1'b0), ._6D(1'b0), ._7D(_74ls283_6_s3), ._0O(ALU_out[8]),
    ._1O(ALU_out[9]), ._2O(ALU_out[10]), ._3O(ALU_out[11]), ._7O(ALU_Lout));  // open: _4O, _5O, _6O
  _74LS541 _74ls541_13 (
    .nOE1(nand_4_out), .nOE2(nand_4_out), ._0D(_74ls283_4_s2), ._1D(_74ls283_4_s3), ._2D(_74ls283_4_s4),
    ._3D(_74ls283_5_s1), ._4D(_74ls283_5_s2), ._5D(_74ls283_5_s3), ._6D(_74ls283_5_s4), ._7D(_74ls283_6_s1),
    ._0O(ALU_out[0]), ._1O(ALU_out[1]), ._2O(ALU_out[2]), ._3O(ALU_out[3]), ._4O(ALU_out[4]),
    ._5O(ALU_out[5]), ._6O(ALU_out[6]), ._7O(ALU_out[7]));
  _74LS541 _74ls541_14 (
    .nOE1(nand_4_out), .nOE2(nand_4_out), ._0D(_74ls283_6_s2), ._1D(_74ls283_6_s3), ._2D(_74ls283_6_s4),
    ._3D(ALU_Lin), ._4D(1'b0), ._5D(1'b0), ._6D(1'b0), ._7D(_74ls283_4_s1), ._0O(ALU_out[8]),
    ._1O(ALU_out[9]), ._2O(ALU_out[10]), ._3O(ALU_out[11]), ._7O(ALU_Lout));  // open: _4O, _5O, _6O
  _74LS541 _74ls541_15 (
    .nOE1(nand_5_out), .nOE2(nand_5_out), ._0D(_74ls283_4_s3), ._1D(_74ls283_4_s4), ._2D(_74ls283_5_s1),
    ._3D(_74ls283_5_s2), ._4D(_74ls283_5_s3), ._5D(_74ls283_5_s4), ._6D(_74ls283_6_s1), ._7D(_74ls283_6_s2),
    ._0O(ALU_out[0]), ._1O(ALU_out[1]), ._2O(ALU_out[2]), ._3O(ALU_out[3]), ._4O(ALU_out[4]),
    ._5O(ALU_out[5]), ._6O(ALU_out[6]), ._7O(ALU_out[7]));
  _74LS541 _74ls541_16 (
    .nOE1(nand_5_out), .nOE2(nand_5_out), ._0D(_74ls283_6_s3), ._1D(_74ls283_6_s4), ._2D(ALU_Lin),
    ._3D(_74ls283_4_s1), ._4D(1'b0), ._5D(1'b0), ._6D(1'b0), ._7D(_74ls283_4_s2), ._0O(ALU_out[8]),
    ._1O(ALU_out[9]), ._2O(ALU_out[10]), ._3O(ALU_out[11]), ._7O(ALU_Lout));  // open: _4O, _5O, _6O

  // Other names for the same wires on the sheet: fAccNegative = ACC[11]; DAW[23:12] = ABUS; DBUS[11:0] = DAW[11:0];
  //   L_GEN (some bits) = {AND, ISZ, DCA, JMS, JMP, IOT, fIndirect, fAutoinc, isCurrPage}; IR0__6[6:0] = IR[6:0];
  //   OPR_SMASPA = IR[6]; OPR_SZASNA = IR[5]; OPR_SNLSZL = IR[4]; OPR_TSTINV = IR[3];
  //   L_OPR1 (some bits) = {CLA_1, CLL, CMA, CML, IAC, BSW};
  //   L_CPU (some bits) = {ION_6001, IOF_6002, GTF_6004, CAF_6007}; INC1_mop1 = ckACC_mop1; ckMQ_2 = ckACC_5;
  //   INC1_jms = ckSetPC_jms; L_OPR2 (some bits) = {CLA_2, HLT}; L_OPR3[11] = CLA_3;
  //   enDBUStoABUS_isz = ckDBUStoABUS_isz; enDBUStoABUS_jmp = ckDBUStoABUS_jmp; enDBUStoABUS_jms = ckDBUStoABUS_jms;
  //   L_IRQ (some bits) = {fGIE, fIrqDly, enIRQ, fKBD, fPRN}; enALUor_2 = enACCtoDBUS_2; enALUtoACC_4 = enACCtoDBUS_2;
  //   enMQtoOBUS_1 = enACCtoDBUS_2; enALUor_3 = CLA_4; enALUtoACC_5 = CLA_4; enMQhold = CLA_4; enMQtoOBUS_2 = CLA_4;
  //   enRAMtoDBUS_0 = ckSetPC_0; enRAMtoDBUS_irq = enPCtoABUS_irq; enRAMtoDBUS_LoadIR = enPCtoABUS_LoadIR;
  //   enSwitchToOBUS = enALUor_mop2; iDone2 = ckIRQhandler; ii_andtad = ckACC_2; INC1_tadand = ckACC_2;
  //   INC1_dca = ii_dca; L_KBD[5:0] = {KCF_6030, KSF_6031, KCC_6032, KRS_6034, KIE_6035, KRB_6036};
  //   LED_MQA = L_OPR3[8]; LED_MQL = L_OPR3[7]; LED_SWP = L_OPR3[9]; MOP = L_GEN[4]; OSR = L_OPR2[1]; RAL = L_OPR1[1];
  //   RAR = L_OPR1[4]; RTF_6005 = L_CPU[2]; RTL = L_OPR1[2]; RTR = L_OPR1[3]; SCA = L_OPR3[10]; SGT_6006 = L_CPU[1];
  //   SKON_6000 = L_CPU[7]; SKP = L_OPR2[8]; SMA = L_OPR2[7]; SNA = L_OPR2[4]; SNL = L_OPR2[3]; SPA = L_OPR2[5];
  //   SRQ_6003 = L_CPU[4]; SZA = L_OPR2[6]; SZL = L_OPR2[2]; TAD = L_GEN[10]; TCF_6042 = L_PRN[3];
  //   TFL_6040 = L_PRN[5]; TLS_6046 = L_PRN[0]; TPC_6044 = L_PRN[2]; TSF_6041 = L_PRN[4]; TSK_6045 = L_PRN[1];
  //   weRAM_isz1 = enIncToDBUS_isz1; weRAM_isz2 = enIncToDBUS_isz2; enPCtoDBUS_jms = ckIncPC_jms1;
  //   weRAM_jms = ckIncPC_jms1

  // Notes on the sheet:
  //   MAX: Hz: 2147483647
  //   SWITCH: default 4095
  //   _25Hz: Hz: 200
  //   in_4: default 1920
  //   clk: Hz: 50
  //   RAM
  //   -----------------
  //   2x 32KB RAM
  //   1x INVERTER
  //   1x OR12
  //   1x OR6
  //   1x OR9
  //   ADDR FROM INSTRUCTION
  //   -----------------
  //   2x 74244 DRIVER
  //   1x INVERTER
  //   5x AND2
  //   1x OR7
  //   DBUS ADDER
  //   -----------------
  //   2x 74374 LATCH
  //   3x 74283 ADDER
  //   3x INVERTER
  //   2x OR3
  //   DBUS->ABUS LATCH
  //   -----------------
  //   2x 74374 LATCH
  //   1x INVERTER
  //   2x OR5
  //   INSTRUCTION REGISTER
  //   INSTRUCTIONS PER SECOND
  //   RAM
  //   DBUS ADDER
  //   Latch at rising C
  //   contents of eeprom_1 (hex, n*v repeats v):
  //   7d,b02,709,664,f02,f02,f02,6*0,800,0,0,fff,7ff,bff,dff,eff,f7f
  //   ,fbf,fdf,0,fef,ff7,ffb,ffd,ffe,0,3ff,1ff,ff,7f,3f,1f,f,7,3,0,1
  //   ,900,97f,555,db6,924,e38,1c7,aaa,249,b6d,a80,4,f02,f02,107,b3a
  //   ,7d4,f02,100,b3e,7cc,9*f02,0,7*f02,118,b52,7c3,f02,128,b56,7ba
  //   ,f02,148,b5a,7b1,31*f02,7e,7a,7b,7c,7d,29c,e80,f08,db6,22a,6ff
  //   ,f20,f02,f08,0,22a,e21,2ff,f20,f02,e80,22b,682,f20,f02,22b,e21
  //   ,282,f20,f02,e80,210,682,f20,f02,282,e20,f20,f02,e80,21e,682,f20
  //   ,f02,282,f20,f02,e80,22c,682,f20,f02,22c,e21,282,f20,f02,e80,22d
  //   ,682,f20,f02,22d,e21,282,f20,f02,e80,22e,6ff,f20,f02,22e,e21,2ff
  //   ,f20,f02,e80,22f,6ff,f20,f02,22f,e21,2ff,f20,f02,e80,230,600,f20
  //   ,f02,230,e21,200,f20,f02,e80,231,600,f20,f02,231,e21,200,f20,f02
  //   ,e80,232,600,f20,f02,232,e21,200,f20,f02,e80,233,600,f20,f02,233
  //   ,e21,200,f20,f02,afd,188,bfc,7a8,e00,f08,e38,e80,322,e21,27f,f20
  //   ,f02,e80,f08,0,210,122,e21,27f,f20,f02,e80,210,600,51e,f02,200
  //   ,f20,f02,e80,37a,e21,27e,f20,f02,e80,210,17a,e21,27e,f20,f02,e80
  //   ,27a,600,51e,f08,f02,200,e21,27a,e20,f20,f02,e80,37b,e21,27a,f20
  //   ,f02,e80,210,17b,e21,27a,f20,f02,e80,27b,600,51e,f08,f02,200,e21
  //   ,27b,e20,f20,f02,e80,37c,e21,27b,f20,f02,e80,210,17c,e21,27b,f20
  //   ,f02,e80,27c,600,51e,f08,f02,200,e21,27c,e20,f20,f02,e80,37d,e21
  //   ,27c,f20,f02,e80,210,17d,e21,27c,f20,f02,e80,27d,600,51e,f08,f02
  //   ,200,e21,27d,e20,f20,f02,aff,188,bfe,79f,e00,e80,37e,e21,27d,f20
  //   ,f02,e80,21e,608,108,208,21d,e20,f20,f02,e80,21d,608,108,208,21e
  //   ,e20,f20,f02,e80,21c,608,708,208,229,e20,f20,f02,e80,21b,608,308
  //   ,e80,208,227,e20,f20,f02,e80,21a,608,108,208,226,e20,f20,f02,e80
  //   ,219,608,108,208,225,e20,f20,f02,e80,217,608,108,208,224,e20,f20
  //   ,f02,e80,216,608,108,208,223,e20,f20,f02,e80,215,608,108,208,222
  //   ,e20,f20,f02,e80,214,608,108,208,221,e20,f20,f02,e80,213,608,108
  //   ,208,220,e20,f20,f02,e80,212,608,508,e00,208,21f,e20,f20,f02,e80
  //   ,211,608,108,208,211,e20,f20,f02,e00,e00,e00,e80,210,608,108,208
  //   ,210,e20,f08,0,f20,f02,e80,21e,609,109,209,21d,e20,f20,f02,e80
  //   ,21d,609,109,209,21e,e20,f20,f02,e80,21c,609,709,209,229,e20,f20
  //   ,f02,e80,21b,609,309,e80,209,227,e20,f20,f02,e80,21a,609,109,209
  //   ,226,e20,f20,f02,e80,219,609,109,209,225,e20,f20,f02,e80,217,609
  //   ,109,209,224,e20,f20,f02,e80,216,609,109,209,223,e20,f20,f02,e80
  //   ,215,609,109,209,222,e20,f20,f02,e80,214,609,109,209,221,e20,f20
  //   ,f02,e80,213,609,109,209,220,e20,f20,f02,e80,212,609,509,e00,209
  //   ,21f,e20,f20,f02,e00,afe,188,bfd,796,e00,e00,e80,211,609,109,209
  //   ,211,e20,f20,f02,e80,210,609,109,209,210,e20,f20,f02,e80,21e,60a
  //   ,10a,20a,21d,e20,f20,f02,e80,21d,60a,10a,20a,21e,e20,f20,f02,e80
  //   ,21c,60a,70a,20a,229,e20,f20,f02,e80,21b,60a,30a,e80,20a,227,e20
  //   ,f20,f02,e80,21a,60a,10a,20a,226,e20,f20,f02,e80,219,60a,10a,20a
  //   ,225,e20,f20,f02,e80,217,60a,10a,20a,224,e20,f20,f02,e80,216,60a
  //   ,10a,20a,223,e20,f20,f02,e80,215,60a,10a,20a,222,e20,f20,f02,e80
  //   ,214,60a,10a,20a,221,e20,f20,f02,e80,213,60a,10a,20a,220,e20,f20
  //   ,f02,e80,212,60a,50a,e00,20a,21f,e20,f20,f02,e80,211,60a,10a,20a
  //   ,211,e20,f20,f02,e80,210,60a,10a,20a,210,e20,f20,f02,e80,21e,60b
  //   ,10b,20b,21d,e20,f20,f02,e80,21d,60b,10b,20b,21e,e20,f20,f02,e80
  //   ,21c,60b,70b,20b,229,e20,f20,f02,e80,21b,60b,30b,e80,20b,227,e20
  //   ,f20,f02,e80,21a,60b,10b,20b,226,e20,f20,f02,e80,219,60b,10b,20b
  //   ,225,e20,f20,f02,e80,217,60b,10b,20b,224,e20,f20,f02,e80,216,60b
  //   ,10b,20b,223,e20,f20,f02,e80,215,60b,10b,20b,222,e20,f20,f02,e80
  //   ,214,60b,10b,20b,221,e20,f20,f02,e80,213,60b,10b,20b,220,e20,f20
  //   ,f02,e80,212,60b,50b,e00,20b,21f,e20,f20,f02,e80,211,60b,10b,20b
  //   ,211,e20,f20,f02,e80,210,60b,10b,20b,210,e20,f20,f02,e80,21e,60c
  //   ,10c,20c,21d,e20,f20,f02,e80,21d,60c,10c,20c,21e,e20,f20,f02,e80
  //   ,21c,60c,70c,20c,229,e20,f20,f02,e80,21b,60c,30c,e80,20c,227,e20
  //   ,f20,f02,e80,21a,60c,10c,20c,226,e20,f20,f02,e80,219,60c,10c,20c
  //   ,225,e20,f20,f02,e80,217,60c,10c,20c,224,e20,f20,f02,e80,216,60c
  //   ,10c,20c,223,e20,f20,f02,e80,215,60c,10c,20c,222,e20,f20,f02,e80
  //   ,214,60c,10c,20c,221,e20,f20,f02,e80,213,60c,10c,20c,220,e20,f20
  //   ,f02,e80,212,60c,50c,e00,20c,21f,e20,f20,f02,e80,211,60c,10c,20c
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  //   contents of CharRom3x (hex, n*v repeats v):
  //   128*483f24cc03cf,128*1483f24cc03cf,128*2483f24cc03cf,128*3483f24cc03cf
  //   ,128*483f03cf4803,128*1483f03cf4803,128*2483f03cf4803,128*3483f03cf4803
  //   ,128*903303bb4833,128*1903303bb4833,128*2903303bb4833,128*3903303bb4833
  //   ,128*3cf00f3483f,128*103cf00f3483f,128*203cf00f3483f,128*303cf00f3483f
  //   ,128*3bb14cc007c,128*103bb14cc007c,128*203bb14cc007c,128*303bb14cc007c
  //   ,128*3c714cc007c,128*103c714cc007c,128*203c714cc007c,128*303c714cc007c
  //   ,513*480300ff4833,257*3c700ff14cc,0,253*3c700ff14cc
  //   OPCODES
  //   AND
  //   INTERRUPT FLAGS
  //   GIE
  //   OPR-1
  //   NOP
  //   OPR-2
  //   CLA
  //   OPR-3
  //   IOT-CPU
  //   SKON
  //   IOT-KEYBOARD
  //   KCF
  //   IOT-PRINTER
  //   TFL
  //   TAD
  //   IRQ
  //   IHBT
  //   SKP
  //   ION
  //   KSF
  //   TSF
  //   ISZ
  //   DCA
  //   IRQ
  //   DLY
  //   INT
  //   BUS
  //   CLL
  //   CMA
  //   SZA
  //   SMA
  //   SCA
  //   SWP
  //   IOF
  //   SRQ
  //   KCC
  //   KRS
  //   TCF
  //   TPC
  //   DBUS->ABUS LATCH
  //   JMS
  //   TTY
  //   IE
  //   CML
  //   SPA
  //   MQA
  //   GTF
  //   KIE
  //   TSK
  //   JMP
  //   KEY
  //   AVAIL
  //   IAC
  //   SNA
  //   MQL
  //   RTF
  //   KRB
  //   TLS
  //   IOT
  //   OPR
  //   PRN
  //   RDY
  //   RAR
  //   RTR
  //   SZL
  //   SNL
  //   LSR
  //   ASL
  //   SGT
  //   CAF
  //   ADDRESS FROM INSTRUCTION
  //   DIR
  //   RAL
  //   OSR
  //   SHL
  //   IND
  //   RTL
  //   HLT
  //   NMI
  //   AUTO
  //   IND
  //   CURR
  //   PAGE
  //   BSW
  //   DVI
  //   MUY
  //   SCL
  //   PC
  //   IR
  //   ACC
  //   MQ
  //   Keyboard Flag
  //   The keyboard flag bit is set when a character has been read into the keyboard buffer. The console-reset or 
  //   power-on operation clears this flag. If interrupts are enabled, this flag generates an interrupt request when set.
  //   Teleprinter Flag
  //   The teleprinter flag bit is set when the character most recently loaded in the teleprinter buffer has been output. 
  //   The console-reset or power-on operation clears this flag. If interrupts are enabled, this flag generates an interrupt 
  //   request when set.
  //   -------------------------------------------------------------------------------------------------------------------------------------------------
  //   6000 - SKON Skip if Interrupt System On
  //   SKON is used to test the state of the interrupt enable flipflop. If interrupts are enabled, the next instruction in sequence is skipped.
  //   6001 - ION Interrupts On
  //   ION is used to turn on interrupts. The effect of this instruction is delayed one instruction so that, for example, an ION instruction 
  //   immediately before a return instruction will not take effect until the return instruction is executed.
  //   6002 - IOF Interrupts Off
  //   IOF is used to turn off or disable interrupts. The effect of this instruction is immediate. In addition, interrupts are disabled immediately 
  //   when an interrupt occurs.
  //   6003 - SRQ Skip on Interrupt Request
  //   SRQ is used to test whether there is a pending interrupt request. If a request is pending, the next instruction in sequence is skipped. 
  //   This test is only meaningful when interrupts are disabled; it may be used, for example, to avoid the expense of an unnecessary return 
  //   from interrupt when some device other than the one just serviced is also requesting service.
  //   6004 - GTF Get Flags
  //   GTF is similar to RIB, but is only available on the PDP-8/E and later models. 
  //   GTF loads the accumulator with various information that may need to be saved and restored during interrupts. 
  //   This includes the link bit, the state of the optional memory management unit, and the greater-than flag from 
  //   the optional extended arithmetic unit. These are packed into the accumulator in the following format:
  //   LINK- the link bit.
  //   GT - the Greater Than bit (see the SGT instruction supported by the extended arithmetic element.
  //   IR - the interrupt request status, as tested by SRQ. This is set to one if an interrupt requesting is pending.
  //   II - the interrupt inhibit bit associated with the Time-Share option of the memory management unit.
  //   IE - the state of the interrupt enable flipflop, as set by the ION and reset by the IOF instructions. This is set to one if interrupts are enabled.
  //   U - the user-mode bit.
  //   IF - the instruction field.
  //   DF - the data field. 
  //   U, IF and DF are the same as the corresponding fields returned by the RIB instruction.
  //   6005 - RTF Restore Flags
  //   RTF restores the state of the flags that are saved by the GTF instruction, using the same data format. 
  //   RTF ignores the IR (interrupt request) bit that was saved by GTF, and the IE (interrupt enable) bit is not fully restored until the 
  //   instruction after the RTF instruction, so that a return from interrupt may be executed before the next interrupt request is serviced.
  //   6006 - SGT Skip if Greater Than
  //   SGT is only supported if the extended arithmetic element is present, This instruction skips if the greater than flag is set.
  //   6007 - CAF Clear All Flags
  //   The effect of the CAF instruction is identical to a master clear issued from the front panel. AC and LINK are cleared, interrupts 
  //   are disabled globally, and all I/O devices are reset. Generally, resetting a device sets the device specific interrupt enable bit 
  //   and terminates any ongoing I/O activity. 
  //   -------------------------------------------------------------------------------------------------------------------------------------------------
  //   6030 - KCF Keyboard Clear Flags
  //   The keyboard flag, signalling input data ready, is cleared.
  //   6031 - KSF Keyboard Skip if Flag
  //   If the keyboard flag is set, indicating that input data is ready, the next instruction in sequence is skipped. 
  //   6032 - KCC Keyboard Clear and read character
  //   The keyboard flag is reset, the accumulator is cleared, and the process of reading the next character of input 
  //   is initiated (in those cases where the interface is connected to a paper-tape reader).
  //   6034 - KRS Keyboard Read Static
  //   The 8-bit character in the keyboard buffer is ored with the accumulator.
  //   6035 - KIE Keyboard Interrupt Enable
  //   The accumulator is loaded into the device control register (the interrupt enable and status report control bits). 
  //   6036 - KRB Keyboard Read and begin next read
  //   The 8 bit character in the keyboard buffer is transferred to the accumulator, and the keyboard flag is cleared, 
  //   allowing the reading of the next character to begin. In effect, this operation combines the KCC and KRS operations.
  //   -------------------------------------------------------------------------------------------------------------------------------------------------
  //   6040 - TFL Teleprinter Flag set
  //   The printer flag, signalling output complete, is set. 
  //   6041 - TSF Teleprinter Skip if Flag
  //   If the printer flag is set, indicating output is complete, the next instruction in sequence is skipped. 
  //   6042 - TCF Teleprinter Clear Flag
  //   The printer flag is reset.
  //   6044 - TPC Teleprinter Print Character
  //   The least significant 8-bits of the accumulator is copied to the print buffer, initiating output.
  //   6045 - TSK Teleprinter Skip
  //   If either the print flag or the keyboard flag are set, the next instruction in sequence is skipped. 
  //   6046 - TLS Teleprinter Load and start
  //   The least significant 8 bits of the accumulator are copied to the print buffer, initiating output, and the printer flag is reset. 
  //   In effect, this operation combines the TCF and TPC operations.
  //   ABUS
  //   DBUS
  //   OBUS
  //   SWITCH
  //   ACCUMULATOR / LINK
  //   PROGRAM COUNTER
  //   RUN/STEP CLOCK
  //   ACCUMULATOR / LINK
  //   -----------------
  //   2x 74273 LATCH
  //   1x 7474 S/R FLIPFLOP
  //   2x 74541 DRIVER
  //   7x INVERTER
  //   1x OR12
  //   2x XOR2
  //   1x AND2
  //   2x OR2
  //   1x OR4
  //   1x OR7
  //   INSTRUCTION DECODER
  //   -----------------
  //   5x 74238 DECODER
  //   2x INVERTER
  //   3x AND2
  //   2x AND3
  //   1x NOR2
  //   PROGRAM COUNTEr
  //   -----------------
  //   3x 74161 COUNTER
  //   4x 74244 DRIVER
  //   5x INVERTER
  //   1x OR3
  //   1x OR4
  //   1x OR2
  //   2x OR2
  //   1x OR4
  //   1x OR7
  //   SWITCH
  //   -----------------
  //   4x 74244 DRIVER
  //   1x INVERTER
  //   INSTRUCTION DECODER
  //   MQ
  //   -----------------
  //   2x 74273 LATCH
  //   2x 74373 DRIVER
  //   2x 74541 DRIVER
  //   2x INVERTER
  //   2x OR2
  //   GRP3 msb1 & lsb1
  //   GRP2 msb1 & lsb0
  //   GRP1 msb0
  //   IR LOAD & PC INCREMENTER
  //   AUTO INDEXER
  //   AND/ADD Accumulator
  //   deposit and clear AC
  //   increment and skip if zero
  //   MOP DECODER
  //   MOP
  //   MOPGRP1
  //   NOP/CLR
  //   load MQ from AC then clear AC
  //   inclusive OR the MQ with the AC
  //   AC=0
  //   AC negative
  //   LINK<>0
  //   SMA      7500  skip on minus AC
  //   SPA      7510  skip on plus AC
  //   SZA      7440  skip on zero AC
  //   SNA      7450  skip on non-zero AC
  //   SNL      7420  skip on non-zero link
  //   SZL      7430  skip on zero link
  //   IOT - CPU IRQ
  //   IOT - TELEPRINTER
  //   IOT - KEYBOARD
  //   ALU
  //   ADD
  //   IAC
  //   PASSTHRU
  //   SWAP
  //   ROT L1
  //   ROT L2
  //   ROT R1
  //   ROT R2
endmodule
